// Digital circuit eater_8bit_relay.dig as structural Verilog
module eater_8bit_relay (
  input  clk,
  input  in_2,
  input  clk_2,
  input  clk_3,
  input  in_5,
  input  clk_4,
  input  MANUAL,
  input  in_8,
  input  in_9,
  input  in_10,
  input  in_11,
  input  in_12,
  input  in_13,
  input  in_14,
  input  in_15,
  input  SELECT,
  input  in_17,
  input  in_18,
  input  in_19,
  input  in_20,
  input  in_21,
  input  in_22,
  input  [7:0] _1,
  input  in_24,
  input  in_25,
  input  [2:0] in_26,
  input  [3:0] _1_2,
  input  in_28,
  input  [2:0] _1_3
);

  wire and_1_out, and_2_out, and_3_out, B_SIGN, CARRY, CE, CLOCK, CO, HALT, J, LRAM, nCLOCK, or_2_out,
       or_3_out, or_4_out, or_5_out, or_6_out, or_7_out, or_9_out, or_10_out, relay_1_p2, relay_2_p2,
       relay_3_p2, relay_4_p2, relay_5_p2, relay_6_p2, relay_7_p2, relay_8_p2, relay_9_p2, relay_10_p3,
       relay_11_p2, relay_12_p2, relay_13_p2, relay_14_p2, relay_15_p4, relay_16_p2, relay_17_p4,
       relay_18_p4, relay_19_p4, relay_20_p4, relay_21_p4, relay_22_p4, relay_23_p4, relay_24_p4,
       relay_25_p4, relay_26_p4, relay_27_p4, relay_28_p4, relay_29_p4, relay_30_p4, relay_31_p4,
       relay_32_p4, relay_33_p4, relay_34_p4, relay_35_p4, relay_36_p4, relay_38_p4, relay_39_p4,
       relay_40_p4, relay_41_p4, relay_42_p4, relay_44_p4, relay_45_p4, relay_46_p4, relay_47_p4,
       relay_48_p4, relay_49_p4, relay_53_p3, relay_53_p4, relay_55_p2, relay_56_p4, relay_57_p3,
       relay_58_p2, relay_59_p4, relay_60_p4, relay_61_p4, relay_63_p2, relay_65_p4, relay_70_p4,
       relay_71_p4, relaydt_1_p7, relaydt_1_p8, relaydt_2_p2, relaydt_3_p8, relaydt_4_p8, relaydt_5_p8,
       relaydt_7_p8, relaydt_9_p3, relaydt_9_p5, relaydt_10_p1, relaydt_10_p4, relaydt_10_p5, relaydt_10_p7,
       relaydt_10_p8, relaydt_10_p10, relaydt_11_p5, relaydt_11_p6, relaydt_13_p4, relaydt_13_p5,
       relaydt_15_p4, relaydt_15_p5, relaydt_17_p3, relaydt_17_p5, relaydt_17_p6, relaydt_18_p4,
       relaydt_18_p5, relaydt_20_p2, relaydt_20_p3, relaydt_21_p8, relaydt_29_p1, relaydt_29_p2,
       relaydt_35_p4, relaydt_35_p6, relaydt_36_p1, relaydt_36_p4, relaydt_36_p5, relaydt_36_p7,
       relaydt_36_p8, relaydt_36_p10, relaydt_43_p1, relaydt_43_p2, relaydt_47_p4, relaydt_47_p6,
       relaydt_52_p1, relaydt_52_p5, relaydt_52_p6, relaydt_52_p8, relaydt_55_p1, relaydt_55_p2,
       relaydt_60_p4, relaydt_60_p5, relaydt_61_p2, relaydt_78_p1, relaydt_78_p4, relaydt_78_p6,
       relaydt_80_p1, relaydt_80_p4, relaydt_80_p6, relaydt_81_p3, relaydt_81_p6, relaydt_81_p9,
       relaydt_81_p12, relaydt_81_p17, relaydt_83_p1, relaydt_83_p4, relaydt_83_p5, relaydt_83_p7,
       relaydt_83_p8, relaydt_83_p10, relaydt_84_p1, relaydt_84_p4, relaydt_84_p5, relaydt_84_p7,
       relaydt_84_p8, relaydt_84_p10, relaydt_85_p4, relaydt_85_p6, relaydt_85_p7, relaydt_90_p3,
       relaydt_90_p5, relaydt_91_p1, relaydt_91_p2, relaydt_92_p1, relaydt_92_p2, relaydt_93_p1,
       relaydt_93_p4, relaydt_93_p5, relaydt_93_p7, relaydt_93_p8, relaydt_93_p10, relaydt_94_p3,
       relaydt_94_p6, relaydt_94_p9, relaydt_94_p14, relaydt_97_p4, relaydt_97_p6, relaydt_99_p4,
       relaydt_99_p6, relaydt_102_p1, relaydt_102_p4, relaydt_102_p5, relaydt_102_p7, relaydt_102_p8,
       relaydt_102_p10, relaydt_103_p1, relaydt_103_p4, relaydt_103_p5, relaydt_103_p7, relaydt_103_p8,
       relaydt_103_p10, relaydt_105_p4, relaydt_105_p6, relaydt_106_p1, relaydt_106_p2, relaydt_107_p1,
       relaydt_107_p4, relaydt_107_p5, relaydt_107_p7, relaydt_107_p8, relaydt_107_p10, relaydt_108_p3,
       relaydt_108_p6, relaydt_108_p9, relaydt_108_p14, relaydt_111_p4, relaydt_111_p6, relaydt_112_p1,
       relaydt_112_p2, relaydt_114_p4, relaydt_114_p6, relaydt_115_p1, relaydt_115_p2, relaydt_117_p4,
       relaydt_117_p6, relaydt_117_p7, relaydt_118_p1, relaydt_118_p4, relaydt_118_p5, relaydt_118_p7,
       relaydt_118_p8, relaydt_118_p10, relaydt_119_p1, relaydt_119_p4, relaydt_119_p5, relaydt_119_p7,
       relaydt_119_p8, relaydt_119_p10, relaydt_122_p1, relaydt_122_p2, relaydt_125_p4, relaydt_125_p6,
       relaydt_126_p3, relaydt_126_p6, relaydt_126_p9, relaydt_126_p14, relaydt_128_p1, relaydt_128_p2,
       relaydt_129_p1, relaydt_129_p2, relaydt_130_p6, relaydt_131_p1, relaydt_131_p4, relaydt_131_p5,
       relaydt_131_p7, relaydt_131_p8, relaydt_131_p10, relaydt_133_p4, relaydt_133_p6, relaydt_135_p4,
       relaydt_135_p6, relaydt_136_p6, relaydt_139_p1, relaydt_139_p4, relaydt_139_p5, relaydt_139_p7,
       relaydt_139_p8, relaydt_139_p10, relaydt_140_p1, relaydt_140_p4, relaydt_140_p5, relaydt_140_p7,
       relaydt_140_p8, relaydt_140_p10, relaydt_141_p6, relaydt_143_p1, relaydt_143_p2, relaydt_144_p3,
       relaydt_144_p6, relaydt_144_p9, relaydt_144_p14, relaydt_149_p4, relaydt_149_p6, relaydt_150_p1,
       relaydt_150_p2, relaydt_151_p1, relaydt_151_p2, relaydt_152_p6, relaydt_154_p1, relaydt_154_p5,
       relaydt_154_p6, relaydt_154_p8, relaydt_156_p4, relaydt_156_p6, relaydt_158_p4, relaydt_158_p6,
       relaydt_159_p6, relaydt_160_p3, relaydt_160_p6, relaydt_160_p9, relaydt_160_p14, relaydt_162_p1,
       relaydt_162_p4, relaydt_162_p5, relaydt_162_p7, relaydt_162_p8, relaydt_162_p10, relaydt_163_p1,
       relaydt_163_p4, relaydt_163_p5, relaydt_163_p7, relaydt_163_p8, relaydt_163_p10, relaydt_164_p6,
       relaydt_167_p1, relaydt_167_p2, relaydt_167_p15, relaydt_168_p6, relaydt_170_p1, relaydt_170_p2,
       relaydt_171_p1, relaydt_171_p2, relaydt_173_p3, relaydt_173_p4, relaydt_174_p3, relaydt_174_p6,
       relaydt_174_p9, relaydt_174_p14, relaydt_177_p4, relaydt_177_p6, relaydt_179_p4, relaydt_179_p6,
       relaydt_183_p1, relaydt_183_p4, relaydt_183_p5, relaydt_183_p7, relaydt_183_p8, relaydt_183_p10,
       relaydt_184_p1, relaydt_184_p4, relaydt_184_p5, relaydt_184_p7, relaydt_184_p8, relaydt_184_p10,
       relaydt_186_p3, relaydt_186_p6, relaydt_186_p9, relaydt_189_p4, relaydt_189_p6, relaydt_190_p1,
       relaydt_190_p2, relaydt_192_p4, relaydt_192_p6, relaydt_193_p1, relaydt_193_p2, relaydt_194_p1,
       relaydt_194_p4, relaydt_194_p5, relaydt_194_p7, relaydt_194_p8, relaydt_194_p10, relaydt_195_p1,
       relaydt_195_p4, relaydt_195_p5, relaydt_195_p7, relaydt_195_p8, relaydt_195_p10, relaydt_196_p11,
       relaydt_196_p12, relaydt_196_p13, relaydt_196_p14, relaydt_199_p1, relaydt_199_p2, relaydt_200_p1,
       relaydt_200_p2, relaydt_201_p1, relaydt_201_p5, relaydt_201_p9, relaydt_201_p13, relaydt_201_p25,
       relaydt_203_p4, relaydt_203_p6, relaydt_205_p4, relaydt_205_p6, relaydt_207_p1, relaydt_207_p5,
       relaydt_207_p6, relaydt_207_p8, relaydt_208_p1, relaydt_208_p5, relaydt_208_p6, relaydt_208_p8,
       relaydt_209_p1, relaydt_209_p2, relaydt_210_p1, relaydt_210_p2, RLB, RLC, RLI, RML, ROL, rs_ff_1_nq,
       rs_ff_1_q, RSB, RSI, SCZL, SRAM, STEP_out, ZERO;
  wire [0:0] relay_20_p5, relaydt_44_p3, relaydt_51_p3, relaydt_53_p3, relaydt_55_p11, relaydt_58_p3,
       relaydt_59_p3, relaydt_64_p3, relaydt_65_p3, relaydt_69_p3, relaydt_70_p3, relaydt_74_p3,
       relaydt_75_p3, relaydt_95_p14, relaydt_109_p3, relaydt_109_p6, relaydt_109_p9, relaydt_109_p14,
       relaydt_123_p1, relaydt_127_p3, relaydt_127_p6, relaydt_127_p9, relaydt_127_p14, relaydt_128_p11,
       relaydt_129_p11, relaydt_143_p11, relaydt_145_p3, relaydt_145_p6, relaydt_145_p9, relaydt_145_p14,
       relaydt_146_p1, relaydt_150_p11, relaydt_151_p11, relaydt_153_p1, relaydt_161_p3, relaydt_161_p6,
       relaydt_161_p9, relaydt_161_p14, relaydt_165_p1, relaydt_167_p11, relaydt_169_p1, relaydt_170_p11,
       relaydt_171_p11, relaydt_172_p1, relaydt_175_p3, relaydt_175_p6, relaydt_175_p9, relaydt_175_p14,
       relaydt_187_p3, relaydt_187_p6, relaydt_187_p10, relaydt_190_p11, relaydt_193_p11, relaydt_199_p11,
       relaydt_200_p11, relaydt_209_p11, relaydt_210_p11;
  wire [1:0] relaydt_19_p2, relaydt_26_p2, relaydt_29_p11, relaydt_82_p3, relaydt_82_p6, relaydt_82_p9,
       relaydt_82_p12, relaydt_91_p11, relaydt_92_p11, relaydt_106_p11, relaydt_137_p1;
  wire [2:0] REG_uCOUNT, relaydt_21_p6, SCZ, uCIncrement;
  wire [3:0] binary_to_bcd_1__1s, binary_to_bcd_1__10s, binary_to_bcd_1__100s, CIncrement, INST, REG_COUNT,
       relaydt_101_p5;
  wire [6:0] REG_B;
  wire [7:0] BUS, REG_C, relaydt_3_p5, relaydt_4_p5, relaydt_5_p5, relaydt_6_p5, relaydt_7_p5, relaydt_86_p5;
  wire [7:6] R1_d;
  wire [15:0] R2_d;

  // RelayDT #(.poles(2)) relaydt_1: pin names not known; wires that end beside it: in_5, clk_3, clk_2, clk, clk_4, 1'b0, relaydt_1_p7, relaydt_1_p8, in_2, relaydt_1_p7, relaydt_1_p8
  // RelayDT relaydt_2: pin names not known; wires that end beside it: 1'b0, relaydt_2_p2
  Button STEP (.out(STEP_out));
  and and_1 (and_1_out, STEP_out, MANUAL, ~HALT);  // And
  RS_FF rs_ff_1 (.S(and_2_out), .C(relaydt_2_p2), .R(~and_2_out), .Q(rs_ff_1_q), .nQ(rs_ff_1_nq));
  or or_1 (CLOCK, and_1_out, rs_ff_1_q);
  and and_2 (and_2_out, ~MANUAL, ~HALT, rs_ff_1_nq);  // And
  not not_1 (nCLOCK, CLOCK);
  LED led_1 (.in(CLOCK));
  LED led_2 (.in(nCLOCK));
  or or_2 (or_2_out, RLB, in_28);
  or or_3 (or_3_out, RLC, in_28);
  or or_4 (or_4_out, RLI, in_28);
  or or_5 (or_5_out, ROL, in_28);
  // Relay relay_1: pin names not known; wires that end beside it: or_2_out, relay_1_p2
  // RelayDT #(.Bits(8)) relaydt_3: pin names not known; wires that end beside it: in_28, {8{1'b0}}, BUS, 1'b0, relaydt_3_p5, CLOCK, 1'b0, relaydt_3_p8, 1'b0
  // Relay relay_2: pin names not known; wires that end beside it: or_3_out, relay_2_p2
  // RelayDT #(.Bits(8)) relaydt_4: pin names not known; wires that end beside it: in_28, {8{1'b0}}, BUS, 1'b0, relaydt_4_p5, CLOCK, 1'b0, relaydt_4_p8, 1'b0
  // Relay relay_3: pin names not known; wires that end beside it: or_4_out, relay_3_p2
  // RelayDT #(.Bits(8)) relaydt_5: pin names not known; wires that end beside it: in_28, {8{1'b0}}, BUS, 1'b0, relaydt_5_p5, CLOCK, 1'b0, relaydt_5_p8, 1'b0
  or or_6 (or_6_out, RML, in_28);
  // RelayDT #(.Bits(8)) relaydt_6: pin names not known; wires that end beside it: in_28, {8{1'b0}}, BUS, 1'b0, relaydt_6_p5, CLOCK, 1'b0
  // Relay relay_4: pin names not known; wires that end beside it: or_5_out, relay_4_p2
  // RelayDT #(.Bits(8)) relaydt_7: pin names not known; wires that end beside it: in_28, {8{1'b0}}, BUS, 1'b0, relaydt_7_p5, CLOCK, 1'b0, relaydt_7_p8, 1'b0
  or or_7 (or_7_out, in_28, and_3_out);
  // RelayDT relaydt_8: pin names not known; wires that end beside it: 1'b0, 1'b1, 1'b0
  // RelayDT relaydt_9: pin names not known; wires that end beside it: 1'b0, 1'b1, relaydt_9_p3, relaydt_9_p3, relaydt_9_p5
  // Relay relay_5: pin names not known; wires that end beside it: relaydt_3_p5[7], relay_5_p2
  // Relay relay_6: pin names not known; wires that end beside it: relaydt_4_p5[7], relay_6_p2
  // Relay relay_7: pin names not known; wires that end beside it: relaydt_5_p5[7], relay_7_p2
  // Relay relay_8: pin names not known; wires that end beside it: or_6_out, relay_8_p2
  // Relay relay_9: pin names not known; wires that end beside it: relaydt_7_p5[7], relay_9_p2
  and and_3 (and_3_out, uCIncrement[0], ~uCIncrement[1], uCIncrement[2]);  // And
  // RelayDT #(.poles(4)) relaydt_10: pin names not known; wires that end beside it: relaydt_10_p1, _1_3[2], relaydt_10_p1, relaydt_10_p4, relaydt_10_p5, 1'b0, relaydt_10_p7, relaydt_10_p8, relaydt_9_p5, relaydt_10_p10, relaydt_10_p10, relaydt_10_p7, relaydt_10_p8
  // RelayDT #(.poles(2)) relaydt_11: pin names not known; wires that end beside it: relay_1_p2, 1'b1, relay_5_p2, 1'b0, relaydt_11_p5, relaydt_11_p6, 1'b0, relaydt_11_p5, 1'b0
  // RelayDT #(.poles(2)) relaydt_12: pin names not known; wires that end beside it: relay_5_p2, B_SIGN, 1'b0, relaydt_11_p6, 1'b1, 1'b0
  LED led_3 (.in(B_SIGN));
  // RelayDT #(.poles(2)) relaydt_13: pin names not known; wires that end beside it: relay_2_p2, 1'b1, relay_6_p2, relaydt_13_p4, relaydt_13_p5, 1'b0, relaydt_13_p4, 1'b0
  // RelayDT #(.poles(2)) relaydt_14: pin names not known; wires that end beside it: relay_6_p2, REG_C[7], 1'b0, relaydt_13_p5, 1'b1, 1'b0
  LED led_4 (.in(REG_C[7]));
  // RelayDT #(.poles(2)) relaydt_15: pin names not known; wires that end beside it: relay_3_p2, 1'b1, relay_7_p2, relaydt_15_p4, relaydt_15_p5, 1'b0, relaydt_15_p4, 1'b0
  // RelayDT #(.poles(2)) relaydt_16: pin names not known; wires that end beside it: relay_7_p2, INST[3], relaydt_15_p5, 1'b1, 1'b0
  LED led_5 (.in(INST[3]));
  // RelayDT #(.poles(2)) relaydt_17: pin names not known; wires that end beside it: relay_8_p2, 1'b1, relaydt_17_p3, 1'b0, relaydt_17_p5, relaydt_17_p6, 1'b0, relaydt_17_p5, 1'b0
  // Relay relay_10: pin names not known; wires that end beside it: relaydt_6_p5[3], 1'b0, relay_10_p3
  // RelayDT #(.poles(2)) relaydt_18: pin names not known; wires that end beside it: relay_4_p2, 1'b1, relay_9_p2, relaydt_18_p4, relaydt_18_p5, 1'b0, relaydt_18_p4, 1'b0
  // RelayDT #(.poles(2)) relaydt_19: pin names not known; wires that end beside it: relay_9_p2, relaydt_19_p2[1], relaydt_18_p5, 1'b1, 1'b0
  // RelayDT #(.poles(2)) relaydt_20: pin names not known; wires that end beside it: 1'b1, relaydt_20_p2, relaydt_20_p3, relaydt_20_p2, 1'b0
  // RelayDT #(.Bits(3)) relaydt_21: pin names not known; wires that end beside it: or_7_out, 3'b000, uCIncrement, nCLOCK, 1'b0, relaydt_21_p6, 1'b0, relaydt_21_p8, 1'b0
  // RelayDT relaydt_22: pin names not known; wires that end beside it: 1'b1, relaydt_3_p8, relaydt_3_p8, 1'b0
  // Relay relay_11: pin names not known; wires that end beside it: relaydt_3_p5[6], relay_11_p2
  // RelayDT relaydt_23: pin names not known; wires that end beside it: 1'b1, relaydt_4_p8, relaydt_4_p8, 1'b0
  // Relay relay_12: pin names not known; wires that end beside it: relaydt_4_p5[6], relay_12_p2
  // RelayDT relaydt_24: pin names not known; wires that end beside it: 1'b1, relaydt_5_p8, relaydt_5_p8, 1'b0
  // Relay relay_13: pin names not known; wires that end beside it: relaydt_5_p5[6], relay_13_p2
  // RelayDT relaydt_25: pin names not known; wires that end beside it: 1'b1, relay_10_p3, relaydt_17_p3, 1'b0
  // RelayDT #(.poles(2)) relaydt_26: pin names not known; wires that end beside it: relay_10_p3, relaydt_26_p2[1], relaydt_17_p6, 1'b1, 1'b0
  LED led_6 (.in(relaydt_26_p2[1]));
  // RelayDT relaydt_27: pin names not known; wires that end beside it: 1'b1, relaydt_7_p8, relaydt_7_p8, 1'b0
  // Relay relay_14: pin names not known; wires that end beside it: relaydt_7_p5[6], relay_14_p2
  // RelayDT relaydt_28: pin names not known; wires that end beside it: 1'b1, relaydt_21_p8
  // RelayDT #(.poles(4)) relaydt_29: pin names not known; wires that end beside it: relaydt_29_p1, relaydt_29_p2, relaydt_9_p5, relaydt_10_p10, relaydt_10_p8, relaydt_29_p1, relaydt_29_p1, relaydt_29_p2, 1'b0, relaydt_10_p4, relaydt_29_p11[1], 1'b1, relaydt_10_p5, REG_uCOUNT[2], 1'b0
  // RelayDT #(.poles(2)) relaydt_30: pin names not known; wires that end beside it: relay_11_p2, relay_11_p2, REG_B[6], 1'b0, relaydt_11_p6, 1'b1, 1'b0
  LED led_7 (.in(REG_B[6]));
  // RelayDT #(.poles(2)) relaydt_31: pin names not known; wires that end beside it: relay_12_p2, relay_12_p2, REG_C[6], 1'b0, relaydt_13_p5, 1'b1, 1'b0
  LED led_8 (.in(REG_C[6]));
  // RelayDT #(.poles(2)) relaydt_32: pin names not known; wires that end beside it: relay_13_p2, relay_13_p2, INST[2], 1'b0, relaydt_15_p5, 1'b1, 1'b0
  LED led_9 (.in(INST[2]));
  // RelayDT #(.poles(2)) relaydt_33: pin names not known; wires that end beside it: relay_14_p2, relay_14_p2, relaydt_19_p2[0], 1'b0, relaydt_18_p5, 1'b1, 1'b0
  // RelayDT relaydt_34: pin names not known; wires that end beside it: relaydt_10_p4, 1'b1, 1'b0
  // RelayDT relaydt_35: pin names not known; wires that end beside it: relaydt_10_p5, 1'b0, 1'b1, relaydt_35_p4, relaydt_35_p4, relaydt_35_p6
  LED led_10 (.in(relaydt_29_p11[1]));
  // Relay relay_15: pin names not known; wires that end beside it: relaydt_17_p3, relaydt_6_p5[2], 1'b0, relay_15_p4
  LED led_11 (.in(relaydt_26_p2[0]));
  // Relay relay_16: pin names not known; wires that end beside it: relaydt_21_p6[2], relay_16_p2
  LED led_12 (.in(REG_uCOUNT[2]));
  // RelayDT #(.poles(4)) relaydt_36: pin names not known; wires that end beside it: relaydt_36_p1, _1_3[1], relaydt_36_p1, relaydt_36_p4, relaydt_36_p5, 1'b0, relaydt_36_p7, relaydt_36_p8, relaydt_35_p6, relaydt_36_p10, relaydt_36_p10, relaydt_36_p7, relaydt_36_p8
  // Relay relay_17: pin names not known; wires that end beside it: relaydt_3_p8, relaydt_3_p5[5], 1'b0, relay_17_p4
  // Relay relay_18: pin names not known; wires that end beside it: relaydt_4_p8, relaydt_4_p5[5], 1'b0, relay_18_p4
  // Relay relay_19: pin names not known; wires that end beside it: relaydt_5_p8, relaydt_5_p5[5], 1'b0, relay_19_p4
  // RelayDT #(.poles(2)) relaydt_37: pin names not known; wires that end beside it: relay_15_p4, relay_15_p4, relaydt_26_p2[0], 1'b0, relaydt_17_p6, 1'b1, 1'b0
  // Relay relay_20: pin names not known; wires that end beside it: relaydt_7_p8, relaydt_7_p5[5], 1'b0, relay_20_p4, relay_20_p5[0]
  // RelayDT #(.poles(2)) relaydt_38: pin names not known; wires that end beside it: relay_16_p2, relay_16_p2, REG_uCOUNT[2], 1'b0, relaydt_20_p3, 1'b1, 1'b0
  // RelayDT #(.poles(2)) relaydt_39: pin names not known; wires that end beside it: relay_17_p4, relay_17_p4, REG_B[5], 1'b0, relaydt_11_p6, 1'b1, 1'b0
  LED led_13 (.in(REG_B[5]));
  // RelayDT #(.poles(2)) relaydt_40: pin names not known; wires that end beside it: relay_18_p4, relay_18_p4, REG_C[5], 1'b0, relaydt_13_p5, 1'b1, 1'b0
  LED led_14 (.in(REG_C[5]));
  // RelayDT #(.poles(2)) relaydt_41: pin names not known; wires that end beside it: relay_19_p4, relay_19_p4, INST[1], 1'b0, relaydt_15_p5, 1'b1, 1'b0
  LED led_15 (.in(INST[1]));
  // Relay relay_21: pin names not known; wires that end beside it: relaydt_17_p3, relaydt_6_p5[1], 1'b0, relay_21_p4
  // RelayDT #(.poles(2)) relaydt_42: pin names not known; wires that end beside it: relay_20_p4, relay_20_p4, relay_20_p5[0], 1'b0, relaydt_18_p5, 1'b1, 1'b0
  // Relay relay_22: pin names not known; wires that end beside it: relaydt_21_p8, relaydt_21_p6[1], 1'b0, relay_22_p4
  // RelayDT #(.poles(4)) relaydt_43: pin names not known; wires that end beside it: relaydt_43_p1, relaydt_43_p2, relaydt_35_p6, relaydt_36_p10, relaydt_36_p8, relaydt_43_p1, relaydt_43_p1, relaydt_43_p2, 1'b0, relaydt_36_p4, relaydt_29_p11[0], 1'b1, relaydt_36_p5, REG_uCOUNT[1], 1'b0
  LED led_16 (.in(relaydt_29_p11[0]));
  // Relay relay_23: pin names not known; wires that end beside it: relaydt_3_p8, relaydt_3_p5[4], 1'b0, relay_23_p4
  // Relay relay_24: pin names not known; wires that end beside it: relaydt_4_p8, relaydt_4_p5[4], 1'b0, relay_24_p4
  // Relay relay_25: pin names not known; wires that end beside it: relaydt_5_p8, relaydt_5_p5[4], 1'b0, relay_25_p4
  // RelayDT #(.poles(2)) relaydt_44: pin names not known; wires that end beside it: relay_21_p4, relay_21_p4, relaydt_44_p3[0], 1'b0, relaydt_17_p6, 1'b1, 1'b0
  LED led_17 (.in(relaydt_44_p3[0]));
  // Relay relay_26: pin names not known; wires that end beside it: relaydt_7_p8, relaydt_7_p5[4], 1'b0, relay_26_p4
  // RelayDT #(.poles(2)) relaydt_45: pin names not known; wires that end beside it: relay_22_p4, relay_22_p4, REG_uCOUNT[1], 1'b0, relaydt_20_p3, 1'b1, 1'b0
  LED led_18 (.in(REG_uCOUNT[1]));
  // RelayDT relaydt_46: pin names not known; wires that end beside it: relaydt_36_p4, 1'b1, 1'b0
  // RelayDT relaydt_47: pin names not known; wires that end beside it: relaydt_36_p5, 1'b0, 1'b1, relaydt_47_p4, relaydt_47_p4, relaydt_47_p6
  // RelayDT #(.poles(2)) relaydt_48: pin names not known; wires that end beside it: relay_23_p4, relay_23_p4, REG_B[4], 1'b0, relaydt_11_p6, 1'b1, 1'b0
  LED led_19 (.in(REG_B[4]));
  // RelayDT #(.poles(2)) relaydt_49: pin names not known; wires that end beside it: relay_24_p4, relay_24_p4, REG_C[4], 1'b0, relaydt_13_p5, 1'b1, 1'b0
  LED led_20 (.in(REG_C[4]));
  // RelayDT #(.poles(2)) relaydt_50: pin names not known; wires that end beside it: relay_25_p4, relay_25_p4, INST[0], 1'b0, relaydt_15_p5, 1'b1, 1'b0
  LED led_21 (.in(INST[0]));
  // RelayDT #(.poles(2)) relaydt_51: pin names not known; wires that end beside it: relay_26_p4, relay_26_p4, relaydt_51_p3[0], 1'b0, relaydt_18_p5, 1'b1, 1'b0
  // RelayDT #(.poles(4)) relaydt_52: pin names not known; wires that end beside it: relaydt_52_p1, _1_3[0], relaydt_52_p1, 1'b0, relaydt_52_p5, relaydt_52_p6, relaydt_47_p6, relaydt_52_p8, relaydt_52_p8, relaydt_52_p5, relaydt_52_p6
  // Relay relay_27: pin names not known; wires that end beside it: relaydt_17_p3, relaydt_6_p5[0], 1'b0, relay_27_p4
  LED led_22 (.in(relaydt_53_p3[0]));
  // Relay relay_28: pin names not known; wires that end beside it: relaydt_21_p8, relaydt_21_p6[0], 1'b0, relay_28_p4
  LED led_23 (.in(REG_uCOUNT[0]));
  // Relay relay_29: pin names not known; wires that end beside it: relaydt_3_p8, relaydt_3_p5[3], 1'b0, relay_29_p4
  // Relay relay_30: pin names not known; wires that end beside it: relaydt_4_p8, relaydt_4_p5[3], 1'b0, relay_30_p4
  // Relay relay_31: pin names not known; wires that end beside it: relaydt_5_p8, relaydt_5_p5[3], 1'b0, relay_31_p4
  // RelayDT #(.poles(2)) relaydt_53: pin names not known; wires that end beside it: relay_27_p4, relay_27_p4, relaydt_53_p3[0], 1'b0, relaydt_17_p6, 1'b1, 1'b0
  // Relay relay_32: pin names not known; wires that end beside it: relaydt_7_p8, relaydt_7_p5[3], 1'b0, relay_32_p4
  // RelayDT #(.poles(2)) relaydt_54: pin names not known; wires that end beside it: relay_28_p4, relay_28_p4, REG_uCOUNT[0], 1'b0, relaydt_20_p3, 1'b1, 1'b0
  // RelayDT #(.poles(4)) relaydt_55: pin names not known; wires that end beside it: relaydt_55_p1, relaydt_55_p2, relaydt_47_p6, relaydt_52_p8, relaydt_52_p6, relaydt_55_p1, relaydt_55_p1, relaydt_55_p2, 1'b0, 1'b1, relaydt_55_p11[0], 1'b1, 1'b0, REG_uCOUNT[0]
  LED led_24 (.in(relaydt_55_p11[0]));
  LED led_25 (.in(BUS[7]));
  // RelayDT #(.poles(2)) relaydt_56: pin names not known; wires that end beside it: relay_29_p4, relay_29_p4, REG_B[3], 1'b0, relaydt_11_p6, 1'b1, 1'b0
  LED led_26 (.in(REG_B[3]));
  // RelayDT #(.poles(2)) relaydt_57: pin names not known; wires that end beside it: relay_30_p4, relay_30_p4, REG_C[3], 1'b0, relaydt_13_p5, 1'b1, 1'b0
  LED led_27 (.in(REG_C[3]));
  // RelayDT #(.poles(2)) relaydt_58: pin names not known; wires that end beside it: relay_31_p4, relay_31_p4, relaydt_58_p3[0], 1'b0, relaydt_15_p5, 1'b1, 1'b0
  LED led_28 (.in(relaydt_58_p3[0]));
  // RelayDT #(.poles(2)) relaydt_59: pin names not known; wires that end beside it: relay_32_p4, relay_32_p4, relaydt_59_p3[0], 1'b0, relaydt_18_p5, 1'b1, 1'b0
  // RelayDT #(.poles(2)) relaydt_60: pin names not known; wires that end beside it: CLOCK, 1'b1, 1'b0, relaydt_60_p4, relaydt_60_p5, relaydt_60_p4, 1'b0
  LED led_29 (.in(BUS[6]));
  LED led_30 (.in(BUS[5]));
  LED led_31 (.in(BUS[4]));
  LED led_32 (.in(BUS[3]));
  // Relay relay_33: pin names not known; wires that end beside it: relaydt_3_p8, relaydt_3_p5[2], 1'b0, relay_33_p4
  // Relay relay_34: pin names not known; wires that end beside it: relaydt_4_p8, relaydt_4_p5[2], 1'b0, relay_34_p4
  // Relay relay_35: pin names not known; wires that end beside it: relaydt_5_p8, relaydt_5_p5[2], 1'b0, relay_35_p4
  // Relay relay_36: pin names not known; wires that end beside it: relaydt_7_p8, relaydt_7_p5[2], 1'b0, relay_36_p4
  // RelayDT relaydt_61: pin names not known; wires that end beside it: 1'b1, relaydt_61_p2
  // Relay #(.Bits(8)) relay_37: pin names not known; wires that end beside it: SELECT, {in_15, in_14, in_13, in_12, in_11, in_10, in_9, in_8}, 1'b0
  LED led_33 (.in(BUS[2]));
  LED led_34 (.in(BUS[1]));
  LED led_35 (.in(BUS[0]));
  // RelayDT #(.poles(2)) relaydt_62: pin names not known; wires that end beside it: relay_33_p4, relay_33_p4, REG_B[2], 1'b0, relaydt_11_p6, 1'b1, 1'b0
  LED led_36 (.in(REG_B[2]));
  // RelayDT #(.poles(2)) relaydt_63: pin names not known; wires that end beside it: relay_34_p4, relay_34_p4, REG_C[2], 1'b0, relaydt_13_p5, 1'b1, 1'b0
  LED led_37 (.in(REG_C[2]));
  // RelayDT #(.poles(2)) relaydt_64: pin names not known; wires that end beside it: relay_35_p4, relay_35_p4, relaydt_64_p3[0], 1'b0, relaydt_15_p5, 1'b1, 1'b0
  LED led_38 (.in(relaydt_64_p3[0]));
  RAMDualPort #(.AddrBits(4), .isProgramMemory("true"), .Bits(16)) R2 (
    .A({relaydt_26_p2, relaydt_44_p3[0], relaydt_53_p3[0]}), .Din({{8{1'b0}}, BUS}), .str(LRAM), .C(CLOCK),
    .ld(1'b1), .D(R2_d));
  LED led_39 (.in(R2_d[6]));
  LED led_40 (.in(R2_d[7]));
  // RelayDT #(.poles(2)) relaydt_65: pin names not known; wires that end beside it: relay_36_p4, relay_36_p4, relaydt_65_p3[0], 1'b0, relaydt_18_p5, 1'b1, 1'b0
  LED led_41 (.in(R2_d[2]));
  LED led_42 (.in(R2_d[3]));
  LED led_43 (.in(R2_d[4]));
  LED led_44 (.in(R2_d[5]));
  Binary_to_BCD binary_to_bcd_1 (
    .In({relaydt_19_p2, relay_20_p5[0], relaydt_51_p3[0], relaydt_59_p3[0], relaydt_65_p3[0], relaydt_70_p3[0], relaydt_75_p3[0]}),
    ._100s(binary_to_bcd_1__100s), ._10s(binary_to_bcd_1__10s), ._1s(binary_to_bcd_1__1s));
  // Relay relay_38: pin names not known; wires that end beside it: relaydt_61_p2, relaydt_29_p11[1], 1'b0, relay_38_p4
  // Relay relay_39: pin names not known; wires that end beside it: relaydt_3_p8, relaydt_3_p5[1], 1'b0, relay_39_p4
  // Relay relay_40: pin names not known; wires that end beside it: relaydt_4_p8, relaydt_4_p5[1], 1'b0, relay_40_p4
  // Relay relay_41: pin names not known; wires that end beside it: relaydt_5_p8, relaydt_5_p5[1], 1'b0, relay_41_p4
  LED led_45 (.in(R2_d[0]));
  LED led_46 (.in(R2_d[1]));
  // Relay relay_42: pin names not known; wires that end beside it: relaydt_7_p8, relaydt_7_p5[1], 1'b0, relay_42_p4
  Seven_Seg_Hex seven_seg_hex_1 (.d(binary_to_bcd_1__100s), .dp(1'b0));
  // RelayDT #(.poles(2)) relaydt_66: pin names not known; wires that end beside it: relay_38_p4, relay_38_p4, uCIncrement[2], 1'b0, relaydt_60_p5, 1'b1, 1'b0
  LED led_47 (.in(uCIncrement[2]));
  // RelayDT #(.poles(2)) relaydt_67: pin names not known; wires that end beside it: relay_39_p4, relay_39_p4, REG_B[1], 1'b0, relaydt_11_p6, 1'b1, 1'b0
  LED led_48 (.in(REG_B[1]));
  // RelayDT #(.poles(2)) relaydt_68: pin names not known; wires that end beside it: relay_40_p4, relay_40_p4, REG_C[1], 1'b0, relaydt_13_p5, 1'b1, 1'b0
  LED led_49 (.in(REG_C[1]));
  // RelayDT #(.poles(2)) relaydt_69: pin names not known; wires that end beside it: relay_41_p4, relay_41_p4, relaydt_69_p3[0], 1'b0, relaydt_15_p5, 1'b1, 1'b0
  LED led_50 (.in(relaydt_69_p3[0]));
  // Relay #(.Bits(8)) relay_43: pin names not known; wires that end beside it: SRAM, R2_d[7:0], 1'b0, BUS
  // RelayDT #(.poles(2)) relaydt_70: pin names not known; wires that end beside it: relay_42_p4, relay_42_p4, relaydt_70_p3[0], 1'b0, relaydt_18_p5, 1'b1, 1'b0
  Seven_Seg_Hex seven_seg_hex_2 (.d(binary_to_bcd_1__10s), .dp(1'b0));
  // Relay relay_44: pin names not known; wires that end beside it: relaydt_61_p2, relaydt_29_p11[0], 1'b0, relay_44_p4
  // Relay relay_45: pin names not known; wires that end beside it: relaydt_3_p8, relaydt_3_p5[0], 1'b0, relay_45_p4
  // Relay relay_46: pin names not known; wires that end beside it: relaydt_4_p8, relaydt_4_p5[0], 1'b0, relay_46_p4
  // Relay relay_47: pin names not known; wires that end beside it: relaydt_5_p8, relaydt_5_p5[0], 1'b0, relay_47_p4
  // Relay relay_48: pin names not known; wires that end beside it: relaydt_7_p8, relaydt_7_p5[0], 1'b0, relay_48_p4
  Seven_Seg_Hex seven_seg_hex_3 (.d(binary_to_bcd_1__1s), .dp(1'b0));
  // RelayDT #(.poles(2)) relaydt_71: pin names not known; wires that end beside it: relay_44_p4, relay_44_p4, uCIncrement[1], 1'b0, relaydt_60_p5, 1'b1, 1'b0
  LED led_51 (.in(uCIncrement[1]));
  // RelayDT #(.poles(2)) relaydt_72: pin names not known; wires that end beside it: relay_45_p4, relay_45_p4, REG_B[0], 1'b0, relaydt_11_p6, 1'b1, 1'b0
  LED led_52 (.in(REG_B[0]));
  // RelayDT #(.poles(2)) relaydt_73: pin names not known; wires that end beside it: relay_46_p4, relay_46_p4, REG_C[0], 1'b0, relaydt_13_p5, 1'b1, 1'b0
  LED led_53 (.in(REG_C[0]));
  // RelayDT #(.poles(2)) relaydt_74: pin names not known; wires that end beside it: relay_47_p4, relay_47_p4, relaydt_74_p3[0], 1'b0, relaydt_15_p5, 1'b1, 1'b0
  LED led_54 (.in(relaydt_74_p3[0]));
  // RelayDT #(.poles(2)) relaydt_75: pin names not known; wires that end beside it: relay_48_p4, relay_48_p4, relaydt_75_p3[0], 1'b0, relaydt_18_p5, 1'b1, 1'b0
  // Relay relay_49: pin names not known; wires that end beside it: relaydt_61_p2, relaydt_55_p11[0], 1'b0, relay_49_p4
  // Relay #(.Bits(8)) relay_50: pin names not known; wires that end beside it: RSB, {B_SIGN, REG_B}, 1'b0, BUS
  // Relay #(.Bits(8)) relay_51: pin names not known; wires that end beside it: in_17, REG_C, 1'b0, BUS
  // Relay #(.Bits(8)) relay_52: pin names not known; wires that end beside it: RSI, {INST, relaydt_58_p3[0], relaydt_64_p3[0], relaydt_69_p3[0], relaydt_74_p3[0]}, 1'b0, BUS
  // RelayDT #(.poles(2)) relaydt_76: pin names not known; wires that end beside it: relay_49_p4, relay_49_p4, uCIncrement[0], 1'b0, relaydt_60_p5, 1'b1, 1'b0
  LED led_55 (.in(uCIncrement[0]));
  LED led_56 (.in(relaydt_82_p3[1]));
  or or_8 (CARRY, relaydt_80_p1, relaydt_78_p1);
  LED led_57 (.in(relaydt_82_p9[1]));
  LED led_58 (.in(relaydt_82_p6[1]));
  // RelayDT relaydt_77: pin names not known; wires that end beside it: 1'b0, 1'b1, 1'b0
  // RelayDT relaydt_78: pin names not known; wires that end beside it: relaydt_78_p1, 1'b0, 1'b1, relaydt_78_p4, relaydt_78_p4, relaydt_78_p6
  // RelayDT relaydt_79: pin names not known; wires that end beside it: 1'b0, 1'b1, 1'b0
  // RelayDT relaydt_80: pin names not known; wires that end beside it: relaydt_80_p1, 1'b0, 1'b1, relaydt_80_p4, relaydt_80_p4, relaydt_80_p6
  // Relay relay_53: pin names not known; wires that end beside it: CLOCK, SCZL, relay_53_p3, relay_53_p4, 1'b0
  // RelayDT #(.poles(4)) relaydt_81: pin names not known; wires that end beside it: 1'b0, 1'b1, relaydt_81_p3, 1'b1, 1'b0, relaydt_81_p6, 1'b0, 1'b1, relaydt_81_p9, 1'b0, 1'b1, relaydt_81_p12, REG_C[7], 1'b0, 1'b0, 1'b1, relaydt_81_p17
  // RelayDT #(.poles(4)) relaydt_82: pin names not known; wires that end beside it: 1'b0, relaydt_81_p3, relaydt_82_p3[1], 1'b1, 1'b0, relaydt_82_p6[1], relaydt_81_p9, relaydt_81_p6, relaydt_82_p9[1], relaydt_81_p12, 1'b1, relaydt_82_p12[1], B_SIGN, 1'b0, 1'b0, relaydt_81_p17, relaydt_82_p3[0]
  LED led_59 (.in(relaydt_82_p12[1]));
  // RelayDT #(.poles(4)) relaydt_83: pin names not known; wires that end beside it: relaydt_83_p1, REG_C[7], relaydt_83_p1, relaydt_83_p4, relaydt_83_p5, 1'b0, relaydt_83_p7, relaydt_83_p8, relaydt_78_p6, relaydt_83_p10, relaydt_83_p10, relaydt_83_p7, relaydt_83_p8
  // RelayDT #(.poles(4)) relaydt_84: pin names not known; wires that end beside it: relaydt_84_p1, _1[7], relaydt_84_p1, relaydt_84_p4, relaydt_84_p5, 1'b0, relaydt_84_p7, relaydt_84_p8, relaydt_80_p6, relaydt_84_p10, relaydt_84_p10, relaydt_84_p7, relaydt_84_p8
  // RelayDT #(.poles(2)) relaydt_85: pin names not known; wires that end beside it: 1'b0, relay_53_p3, 1'b1, relaydt_85_p4, 1'b0, relaydt_85_p6, relaydt_85_p7, 1'b0, relaydt_85_p6, 1'b0
  // Relay relay_54: pin names not known; wires that end beside it: B_SIGN, relaydt_85_p4
  LED Sign (.in(SCZ[2]));
  // RelayDT #(.Bits(8)) relaydt_86: pin names not known; wires that end beside it: in_28, {8{1'b0}}, BUS, 1'b0, relaydt_86_p5
  LED led_60 (.in(HALT));
  LED led_61 (.in(relaydt_82_p3[0]));
  // RelayDT relaydt_87: pin names not known; wires that end beside it: 1'b1, relay_53_p4, relay_53_p4, 1'b0
  // RelayDT #(.poles(2)) relaydt_88: pin names not known; wires that end beside it: relaydt_85_p4, SCZ[2], relaydt_85_p7, 1'b1, 1'b0
  or or_9 (or_9_out, J, in_28);
  // RelayDT relaydt_89: pin names not known; wires that end beside it: 1'b0, 1'b1, 1'b0
  // RelayDT relaydt_90: pin names not known; wires that end beside it: 1'b0, 1'b1, relaydt_90_p3, relaydt_90_p3, relaydt_90_p5
  LED led_62 (.in(RML));
  LED led_63 (.in(LRAM));
  LED led_64 (.in(relaydt_82_p9[0]));
  LED led_65 (.in(relaydt_82_p6[0]));
  // RelayDT #(.poles(4)) relaydt_91: pin names not known; wires that end beside it: relaydt_91_p1, relaydt_91_p2, relaydt_78_p6, relaydt_83_p10, relaydt_83_p8, relaydt_91_p1, relaydt_91_p1, relaydt_91_p2, 1'b0, relaydt_83_p4, relaydt_91_p11[1], 1'b1, relaydt_83_p5, B_SIGN, 1'b0
  LED led_66 (.in(relaydt_91_p11[1]));
  // RelayDT #(.poles(4)) relaydt_92: pin names not known; wires that end beside it: relaydt_92_p1, relaydt_92_p2, relaydt_80_p6, relaydt_84_p10, relaydt_84_p8, relaydt_92_p1, relaydt_92_p1, relaydt_92_p2, 1'b0, relaydt_84_p4, relaydt_92_p11[1], 1'b1, relaydt_84_p5, B_SIGN, 1'b0
  LED led_67 (.in(relaydt_92_p11[1]));
  // Relay relay_55: pin names not known; wires that end beside it: CARRY, relay_55_p2
  or or_10 (or_10_out, CE, in_28, or_9_out);
  // RelayDT #(.poles(4)) relaydt_93: pin names not known; wires that end beside it: relaydt_93_p1, _1_2[3], relaydt_93_p1, relaydt_93_p4, relaydt_93_p5, 1'b0, relaydt_93_p7, relaydt_93_p8, relaydt_90_p5, relaydt_93_p10, relaydt_93_p10, relaydt_93_p7, relaydt_93_p8
  LED led_68 (.in(SRAM));
  // RelayDT #(.poles(4)) relaydt_94: pin names not known; wires that end beside it: 1'b1, 1'b0, relaydt_94_p3, 1'b0, 1'b1, relaydt_94_p6, 1'b0, 1'b1, relaydt_94_p9, REG_C[6], 1'b0, 1'b0, 1'b1, relaydt_94_p14
  // RelayDT #(.poles(4)) relaydt_95: pin names not known; wires that end beside it: 1'b1, 1'b0, relaydt_82_p6[0], relaydt_94_p6, relaydt_94_p3, relaydt_82_p9[0], relaydt_94_p9, 1'b1, relaydt_82_p12[0], REG_B[6], 1'b0, 1'b0, relaydt_94_p14, relaydt_95_p14[0]
  LED led_69 (.in(relaydt_82_p12[0]));
  // RelayDT relaydt_96: pin names not known; wires that end beside it: relaydt_83_p4, 1'b1, 1'b0
  // RelayDT relaydt_97: pin names not known; wires that end beside it: relaydt_83_p5, 1'b0, 1'b1, relaydt_97_p4, relaydt_97_p4, relaydt_97_p6
  // RelayDT relaydt_98: pin names not known; wires that end beside it: relaydt_84_p4, 1'b1, 1'b0
  // RelayDT relaydt_99: pin names not known; wires that end beside it: relaydt_84_p5, 1'b0, 1'b1, relaydt_99_p4, relaydt_99_p4, relaydt_99_p6
  // RelayDT #(.poles(2)) relaydt_100: pin names not known; wires that end beside it: relay_55_p2, relay_55_p2, SCZ[1], 1'b0, relaydt_85_p7, 1'b1, 1'b0
  LED u_Carry (.in(SCZ[1]));
  // RelayDT #(.Bits(4)) relaydt_101: pin names not known; wires that end beside it: or_9_out, relaydt_86_p5[3:0], CIncrement, 1'b0, relaydt_101_p5
  LED led_70 (.in(RSI));
  LED led_71 (.in(relaydt_95_p14[0]));
  // RelayDT #(.poles(4)) relaydt_102: pin names not known; wires that end beside it: relaydt_102_p1, REG_C[6], relaydt_102_p1, relaydt_102_p4, relaydt_102_p5, 1'b0, relaydt_102_p7, relaydt_102_p8, relaydt_97_p6, relaydt_102_p10, relaydt_102_p10, relaydt_102_p7, relaydt_102_p8
  // RelayDT #(.poles(4)) relaydt_103: pin names not known; wires that end beside it: relaydt_103_p1, _1[6], relaydt_103_p1, relaydt_103_p4, relaydt_103_p5, 1'b0, relaydt_103_p7, relaydt_103_p8, relaydt_99_p6, relaydt_103_p10, relaydt_103_p10, relaydt_103_p7, relaydt_103_p8
  // RelayDT relaydt_104: pin names not known; wires that end beside it: relaydt_93_p4, 1'b1, 1'b0
  // RelayDT relaydt_105: pin names not known; wires that end beside it: relaydt_93_p5, 1'b0, 1'b1, relaydt_105_p4, relaydt_105_p4, relaydt_105_p6
  // RelayDT #(.poles(4)) relaydt_106: pin names not known; wires that end beside it: relaydt_106_p1, relaydt_106_p2, relaydt_90_p5, relaydt_93_p10, relaydt_93_p8, relaydt_106_p1, relaydt_106_p1, relaydt_106_p2, 1'b0, relaydt_93_p4, relaydt_106_p11[1], 1'b1, relaydt_93_p5, REG_COUNT[3], 1'b0
  LED led_72 (.in(relaydt_106_p11[1]));
  EEPROMDualPort #(.AddrBits(10), .isProgramMemory("true"), .Bits(16)) R1 (
    .A({SCZ, INST, REG_uCOUNT}), .Din({16{1'b0}}), .str(1'b0), .C(CLOCK), .ld(1'b1),
    .D({HALT, RML, LRAM, SRAM, RSI, RLI, RLB, RSB, R1_d, RLC, ROL, CE, CO, J, SCZL}));
  LED led_73 (.in(RLI));
  LED led_74 (.in(RLB));
  LED led_75 (.in(relaydt_109_p6[0]));
  LED led_76 (.in(relaydt_109_p3[0]));
  // Relay relay_56: pin names not known; wires that end beside it: relay_53_p4, ZERO, 1'b0, relay_56_p4
  LED u_Zero (.in(SCZ[0]));
  // Relay relay_57: pin names not known; wires that end beside it: CLOCK, or_10_out, relay_57_p3
  // RelayDT #(.poles(4)) relaydt_107: pin names not known; wires that end beside it: relaydt_107_p1, _1_2[2], relaydt_107_p1, relaydt_107_p4, relaydt_107_p5, 1'b0, relaydt_107_p7, relaydt_107_p8, relaydt_105_p6, relaydt_107_p10, relaydt_107_p10, relaydt_107_p7, relaydt_107_p8
  LED led_77 (.in(RSB));
  // RelayDT #(.poles(4)) relaydt_108: pin names not known; wires that end beside it: 1'b1, 1'b0, relaydt_108_p3, 1'b0, 1'b1, relaydt_108_p6, 1'b0, 1'b1, relaydt_108_p9, REG_C[5], 1'b0, 1'b0, 1'b1, relaydt_108_p14
  // RelayDT #(.poles(4)) relaydt_109: pin names not known; wires that end beside it: 1'b1, 1'b0, relaydt_109_p3[0], relaydt_108_p6, relaydt_108_p3, relaydt_109_p6[0], relaydt_108_p9, 1'b1, relaydt_109_p9[0], REG_B[5], 1'b0, 1'b0, relaydt_108_p14, relaydt_109_p14[0]
  LED led_78 (.in(relaydt_109_p9[0]));
  // RelayDT relaydt_110: pin names not known; wires that end beside it: relaydt_102_p4, 1'b1, 1'b0
  // RelayDT relaydt_111: pin names not known; wires that end beside it: relaydt_102_p5, 1'b0, 1'b1, relaydt_111_p4, relaydt_111_p4, relaydt_111_p6
  // RelayDT #(.poles(4)) relaydt_112: pin names not known; wires that end beside it: relaydt_112_p1, relaydt_112_p2, relaydt_97_p6, relaydt_102_p10, relaydt_102_p8, relaydt_112_p1, relaydt_112_p1, relaydt_112_p2, 1'b0, relaydt_102_p4, relaydt_91_p11[0], 1'b1, relaydt_102_p5, REG_B[6], 1'b0
  LED led_79 (.in(relaydt_91_p11[0]));
  // RelayDT relaydt_113: pin names not known; wires that end beside it: relaydt_103_p4, 1'b1, 1'b0
  // RelayDT relaydt_114: pin names not known; wires that end beside it: relaydt_103_p5, 1'b0, 1'b1, relaydt_114_p4, relaydt_114_p4, relaydt_114_p6
  // RelayDT #(.poles(4)) relaydt_115: pin names not known; wires that end beside it: relaydt_115_p1, relaydt_115_p2, relaydt_99_p6, relaydt_103_p10, relaydt_103_p8, relaydt_115_p1, relaydt_115_p1, relaydt_115_p2, 1'b0, relaydt_103_p4, relaydt_92_p11[0], 1'b1, relaydt_103_p5, REG_B[6], 1'b0
  LED led_80 (.in(relaydt_92_p11[0]));
  // RelayDT #(.poles(2)) relaydt_116: pin names not known; wires that end beside it: relay_56_p4, relay_56_p4, SCZ[0], 1'b0, relaydt_85_p7, 1'b1, 1'b0
  // RelayDT #(.poles(2)) relaydt_117: pin names not known; wires that end beside it: 1'b0, relay_57_p3, 1'b1, relaydt_117_p4, 1'b0, relaydt_117_p6, relaydt_117_p7, 1'b0, relaydt_117_p6, 1'b0
  // Relay relay_58: pin names not known; wires that end beside it: relaydt_101_p5[3], relay_58_p2
  LED led_81 (.in(relaydt_109_p14[0]));
  // RelayDT #(.poles(4)) relaydt_118: pin names not known; wires that end beside it: relaydt_118_p1, REG_C[5], relaydt_118_p1, relaydt_118_p4, relaydt_118_p5, 1'b0, relaydt_118_p7, relaydt_118_p8, relaydt_111_p6, relaydt_118_p10, relaydt_118_p10, relaydt_118_p7, relaydt_118_p8
  // RelayDT #(.poles(4)) relaydt_119: pin names not known; wires that end beside it: relaydt_119_p1, _1[5], relaydt_119_p1, relaydt_119_p4, relaydt_119_p5, 1'b0, relaydt_119_p7, relaydt_119_p8, relaydt_114_p6, relaydt_119_p10, relaydt_119_p10, relaydt_119_p7, relaydt_119_p8
  // RelayDT relaydt_120: pin names not known; wires that end beside it: 1'b1, relay_58_p2, relaydt_117_p4, 1'b0
  // RelayDT #(.poles(2)) relaydt_121: pin names not known; wires that end beside it: relay_58_p2, REG_COUNT[3], relaydt_117_p7, 1'b1, 1'b0
  LED led_82 (.in(REG_COUNT[3]));
  // RelayDT #(.poles(4)) relaydt_122: pin names not known; wires that end beside it: relaydt_122_p1, relaydt_122_p2, relaydt_105_p6, relaydt_107_p10, relaydt_107_p8, relaydt_122_p1, relaydt_122_p1, relaydt_122_p2, 1'b0, relaydt_107_p4, relaydt_106_p11[0], 1'b1, relaydt_107_p5, REG_COUNT[2], 1'b0
  LED led_83 (.in(RLC));
  LED led_84 (.in(relaydt_127_p6[0]));
  LED led_85 (.in(relaydt_127_p3[0]));
  // RelayDT relaydt_123: pin names not known; wires that end beside it: relaydt_123_p1[0], 1'b1, 1'b0
  // RelayDT relaydt_124: pin names not known; wires that end beside it: relaydt_107_p4, 1'b1, 1'b0
  // RelayDT relaydt_125: pin names not known; wires that end beside it: relaydt_107_p5, 1'b0, 1'b1, relaydt_125_p4, relaydt_125_p4, relaydt_125_p6
  LED led_86 (.in(relaydt_106_p11[0]));
  LED led_87 (.in(ROL));
  // RelayDT #(.poles(4)) relaydt_126: pin names not known; wires that end beside it: 1'b1, 1'b0, relaydt_126_p3, 1'b0, 1'b1, relaydt_126_p6, 1'b0, 1'b1, relaydt_126_p9, REG_C[4], 1'b0, 1'b0, 1'b1, relaydt_126_p14
  // RelayDT #(.poles(4)) relaydt_127: pin names not known; wires that end beside it: 1'b1, 1'b0, relaydt_127_p3[0], relaydt_126_p6, relaydt_126_p3, relaydt_127_p6[0], relaydt_126_p9, 1'b1, relaydt_127_p9[0], REG_B[4], 1'b0, 1'b0, relaydt_126_p14, relaydt_127_p14[0]
  LED led_88 (.in(relaydt_127_p9[0]));
  // RelayDT #(.poles(4)) relaydt_128: pin names not known; wires that end beside it: relaydt_128_p1, relaydt_128_p2, relaydt_111_p6, relaydt_118_p10, relaydt_118_p8, relaydt_128_p1, relaydt_128_p1, relaydt_128_p2, 1'b0, relaydt_118_p4, relaydt_128_p11[0], 1'b1, relaydt_118_p5, REG_B[5], 1'b0
  // RelayDT #(.poles(4)) relaydt_129: pin names not known; wires that end beside it: relaydt_129_p1, relaydt_129_p2, relaydt_114_p6, relaydt_119_p10, relaydt_119_p8, relaydt_129_p1, relaydt_129_p1, relaydt_129_p2, 1'b0, relaydt_119_p4, relaydt_129_p11[0], 1'b1, relaydt_119_p5, REG_B[5], 1'b0
  // RelayDT relaydt_130: pin names not known; wires that end beside it: B_SIGN, 1'b0, 1'b1, B_SIGN, 1'b0, relaydt_130_p6, 1'b0
  LED led_89 (.in(relaydt_137_p1[1]));
  // Relay relay_59: pin names not known; wires that end beside it: relaydt_117_p4, relaydt_101_p5[2], 1'b0, relay_59_p4
  // RelayDT #(.poles(4)) relaydt_131: pin names not known; wires that end beside it: relaydt_131_p1, _1_2[1], relaydt_131_p1, relaydt_131_p4, relaydt_131_p5, 1'b0, relaydt_131_p7, relaydt_131_p8, relaydt_125_p6, relaydt_131_p10, relaydt_131_p10, relaydt_131_p7, relaydt_131_p8
  LED led_90 (.in(CE));
  LED led_91 (.in(relaydt_127_p14[0]));
  // RelayDT relaydt_132: pin names not known; wires that end beside it: relaydt_118_p4, 1'b1, 1'b0
  // RelayDT relaydt_133: pin names not known; wires that end beside it: relaydt_118_p5, 1'b0, 1'b1, relaydt_133_p4, relaydt_133_p4, relaydt_133_p6
  LED led_92 (.in(relaydt_128_p11[0]));
  // RelayDT relaydt_134: pin names not known; wires that end beside it: relaydt_119_p4, 1'b1, 1'b0
  // RelayDT relaydt_135: pin names not known; wires that end beside it: relaydt_119_p5, 1'b0, 1'b1, relaydt_135_p4, relaydt_135_p4, relaydt_135_p6
  LED led_93 (.in(relaydt_129_p11[0]));
  // RelayDT relaydt_136: pin names not known; wires that end beside it: REG_B[6], 1'b0, relaydt_130_p6, REG_B[6], 1'b0, relaydt_136_p6, 1'b0
  // RelayDT relaydt_137: pin names not known; wires that end beside it: relaydt_137_p1[1], 1'b1, 1'b0
  LED led_94 (.in(relaydt_137_p1[0]));
  // RelayDT #(.poles(2)) relaydt_138: pin names not known; wires that end beside it: relay_59_p4, relay_59_p4, REG_COUNT[2], 1'b0, relaydt_117_p7, 1'b1, 1'b0
  LED led_95 (.in(REG_COUNT[2]));
  LED led_96 (.in(CO));
  LED led_97 (.in(J));
  LED led_98 (.in(relaydt_145_p6[0]));
  LED led_99 (.in(relaydt_145_p3[0]));
  // RelayDT #(.poles(4)) relaydt_139: pin names not known; wires that end beside it: relaydt_139_p1, REG_C[4], relaydt_139_p1, relaydt_139_p4, relaydt_139_p5, 1'b0, relaydt_139_p7, relaydt_139_p8, relaydt_133_p6, relaydt_139_p10, relaydt_139_p10, relaydt_139_p7, relaydt_139_p8
  // RelayDT #(.poles(4)) relaydt_140: pin names not known; wires that end beside it: relaydt_140_p1, _1[4], relaydt_140_p1, relaydt_140_p4, relaydt_140_p5, 1'b0, relaydt_140_p7, relaydt_140_p8, relaydt_135_p6, relaydt_140_p10, relaydt_140_p10, relaydt_140_p7, relaydt_140_p8
  // RelayDT relaydt_141: pin names not known; wires that end beside it: REG_B[5], 1'b0, relaydt_136_p6, REG_B[5], 1'b0, relaydt_141_p6, 1'b0
  // RelayDT relaydt_142: pin names not known; wires that end beside it: relaydt_137_p1[0], 1'b1, 1'b0
  LED led_100 (.in(relaydt_146_p1[0]));
  // Relay relay_60: pin names not known; wires that end beside it: relaydt_117_p4, relaydt_101_p5[1], 1'b0, relay_60_p4
  // RelayDT #(.poles(4)) relaydt_143: pin names not known; wires that end beside it: relaydt_143_p1, relaydt_143_p2, relaydt_125_p6, relaydt_131_p10, relaydt_131_p8, relaydt_143_p1, relaydt_143_p1, relaydt_143_p2, 1'b0, relaydt_131_p4, relaydt_143_p11[0], 1'b1, relaydt_131_p5, REG_COUNT[1], 1'b0
  LED led_101 (.in(SCZL));
  // RelayDT #(.poles(4)) relaydt_144: pin names not known; wires that end beside it: 1'b1, 1'b0, relaydt_144_p3, 1'b0, 1'b1, relaydt_144_p6, 1'b0, 1'b1, relaydt_144_p9, REG_C[3], 1'b0, 1'b0, 1'b1, relaydt_144_p14
  // RelayDT #(.poles(4)) relaydt_145: pin names not known; wires that end beside it: 1'b1, 1'b0, relaydt_145_p3[0], relaydt_144_p6, relaydt_144_p3, relaydt_145_p6[0], relaydt_144_p9, 1'b1, relaydt_145_p9[0], REG_B[3], 1'b0, 1'b0, relaydt_144_p14, relaydt_145_p14[0]
  LED led_102 (.in(relaydt_145_p9[0]));
  // RelayDT relaydt_146: pin names not known; wires that end beside it: relaydt_146_p1[0], 1'b1, 1'b0
  LED led_103 (.in(relaydt_153_p1[0]));
  // RelayDT #(.poles(2)) relaydt_147: pin names not known; wires that end beside it: relay_60_p4, relay_60_p4, REG_COUNT[1], 1'b0, relaydt_117_p7, 1'b1, 1'b0
  LED led_104 (.in(REG_COUNT[1]));
  // RelayDT relaydt_148: pin names not known; wires that end beside it: relaydt_131_p4, 1'b1, 1'b0
  // RelayDT relaydt_149: pin names not known; wires that end beside it: relaydt_131_p5, 1'b0, 1'b1, relaydt_149_p4, relaydt_149_p4, relaydt_149_p6
  LED led_105 (.in(relaydt_143_p11[0]));
  LED led_106 (.in(relaydt_145_p14[0]));
  // RelayDT #(.poles(4)) relaydt_150: pin names not known; wires that end beside it: relaydt_150_p1, relaydt_150_p2, relaydt_133_p6, relaydt_139_p10, relaydt_139_p8, relaydt_150_p1, relaydt_150_p1, relaydt_150_p2, 1'b0, relaydt_139_p4, relaydt_150_p11[0], 1'b1, relaydt_139_p5, REG_B[4], 1'b0
  // RelayDT #(.poles(4)) relaydt_151: pin names not known; wires that end beside it: relaydt_151_p1, relaydt_151_p2, relaydt_135_p6, relaydt_140_p10, relaydt_140_p8, relaydt_151_p1, relaydt_151_p1, relaydt_151_p2, 1'b0, relaydt_140_p4, relaydt_151_p11[0], 1'b1, relaydt_140_p5, REG_B[4], 1'b0
  // RelayDT relaydt_152: pin names not known; wires that end beside it: REG_B[4], 1'b0, relaydt_141_p6, REG_B[4], 1'b0, relaydt_152_p6, 1'b0
  // RelayDT relaydt_153: pin names not known; wires that end beside it: relaydt_153_p1[0], 1'b1, 1'b0
  // RelayDT #(.poles(4)) relaydt_154: pin names not known; wires that end beside it: relaydt_154_p1, _1_2[0], relaydt_154_p1, 1'b0, relaydt_154_p5, relaydt_154_p6, relaydt_149_p6, relaydt_154_p8, relaydt_154_p8, relaydt_154_p5, relaydt_154_p6
  LED led_107 (.in(relaydt_161_p6[0]));
  LED led_108 (.in(relaydt_161_p3[0]));
  // RelayDT relaydt_155: pin names not known; wires that end beside it: relaydt_139_p4, 1'b1, 1'b0
  // RelayDT relaydt_156: pin names not known; wires that end beside it: relaydt_139_p5, 1'b0, 1'b1, relaydt_156_p4, relaydt_156_p4, relaydt_156_p6
  LED led_109 (.in(relaydt_150_p11[0]));
  // RelayDT relaydt_157: pin names not known; wires that end beside it: relaydt_140_p4, 1'b1, 1'b0
  // RelayDT relaydt_158: pin names not known; wires that end beside it: relaydt_140_p5, 1'b0, 1'b1, relaydt_158_p4, relaydt_158_p4, relaydt_158_p6
  LED led_110 (.in(relaydt_151_p11[0]));
  // RelayDT relaydt_159: pin names not known; wires that end beside it: REG_B[3], 1'b0, relaydt_152_p6, REG_B[3], 1'b0, relaydt_159_p6, 1'b0
  LED led_111 (.in(relaydt_165_p1[0]));
  // Relay relay_61: pin names not known; wires that end beside it: relaydt_117_p4, relaydt_101_p5[0], 1'b0, relay_61_p4
  // RelayDT #(.poles(4)) relaydt_160: pin names not known; wires that end beside it: 1'b1, 1'b0, relaydt_160_p3, 1'b0, 1'b1, relaydt_160_p6, 1'b0, 1'b1, relaydt_160_p9, REG_C[2], 1'b0, 1'b0, 1'b1, relaydt_160_p14
  // RelayDT #(.poles(4)) relaydt_161: pin names not known; wires that end beside it: 1'b1, 1'b0, relaydt_161_p3[0], relaydt_160_p6, relaydt_160_p3, relaydt_161_p6[0], relaydt_160_p9, 1'b1, relaydt_161_p9[0], REG_B[2], 1'b0, 1'b0, relaydt_160_p14, relaydt_161_p14[0]
  LED led_112 (.in(relaydt_161_p9[0]));
  // RelayDT #(.poles(4)) relaydt_162: pin names not known; wires that end beside it: relaydt_162_p1, REG_C[3], relaydt_162_p1, relaydt_162_p4, relaydt_162_p5, 1'b0, relaydt_162_p7, relaydt_162_p8, relaydt_156_p6, relaydt_162_p10, relaydt_162_p10, relaydt_162_p7, relaydt_162_p8
  // RelayDT #(.poles(4)) relaydt_163: pin names not known; wires that end beside it: relaydt_163_p1, _1[3], relaydt_163_p1, relaydt_163_p4, relaydt_163_p5, 1'b0, relaydt_163_p7, relaydt_163_p8, relaydt_158_p6, relaydt_163_p10, relaydt_163_p10, relaydt_163_p7, relaydt_163_p8
  // RelayDT relaydt_164: pin names not known; wires that end beside it: REG_B[2], 1'b0, relaydt_159_p6, REG_B[2], 1'b0, relaydt_164_p6, 1'b0
  // RelayDT relaydt_165: pin names not known; wires that end beside it: relaydt_165_p1[0], 1'b1, 1'b0
  LED led_113 (.in(relaydt_169_p1[0]));
  // RelayDT #(.poles(2)) relaydt_166: pin names not known; wires that end beside it: relay_61_p4, relay_61_p4, REG_COUNT[0], 1'b0, relaydt_117_p7, 1'b1, 1'b0, CO, 1'b0
  LED led_114 (.in(REG_COUNT[0]));
  // RelayDT #(.poles(4)) relaydt_167: pin names not known; wires that end beside it: relaydt_167_p1, relaydt_167_p2, relaydt_149_p6, relaydt_154_p8, relaydt_154_p6, relaydt_167_p1, relaydt_167_p1, relaydt_167_p2, 1'b0, 1'b1, relaydt_167_p11[0], 1'b1, 1'b0, REG_COUNT[0], relaydt_167_p15, 1'b0
  LED led_115 (.in(relaydt_167_p11[0]));
  LED led_116 (.in(relaydt_161_p14[0]));
  // RelayDT relaydt_168: pin names not known; wires that end beside it: REG_B[1], 1'b0, relaydt_164_p6, REG_B[1], 1'b0, relaydt_168_p6, 1'b0
  // RelayDT relaydt_169: pin names not known; wires that end beside it: relaydt_169_p1[0], 1'b1, 1'b0
  LED led_117 (.in(relaydt_172_p1[0]));
  LED led_118 (.in(relaydt_175_p6[0]));
  LED led_119 (.in(relaydt_175_p3[0]));
  // RelayDT #(.poles(4)) relaydt_170: pin names not known; wires that end beside it: relaydt_170_p1, relaydt_170_p2, relaydt_156_p6, relaydt_162_p10, relaydt_162_p8, relaydt_170_p1, relaydt_170_p1, relaydt_170_p2, 1'b0, relaydt_162_p4, relaydt_170_p11[0], 1'b1, relaydt_162_p5, REG_B[3], 1'b0
  LED led_120 (.in(relaydt_170_p11[0]));
  // RelayDT #(.poles(4)) relaydt_171: pin names not known; wires that end beside it: relaydt_171_p1, relaydt_171_p2, relaydt_158_p6, relaydt_163_p10, relaydt_163_p8, relaydt_171_p1, relaydt_171_p1, relaydt_171_p2, 1'b0, relaydt_163_p4, relaydt_171_p11[0], 1'b1, relaydt_163_p5, REG_B[3], 1'b0
  LED led_121 (.in(relaydt_171_p11[0]));
  // RelayDT relaydt_172: pin names not known; wires that end beside it: relaydt_172_p1[0], 1'b1, 1'b0
  LED led_122 (.in(relaydt_123_p1[0]));
  // Relay #(.Bits(8)) relay_62: pin names not known; wires that end beside it: {4'b0000, REG_COUNT}, 1'b0, BUS
  // RelayDT #(.poles(2)) relaydt_173: pin names not known; wires that end beside it: nCLOCK, 1'b1, relaydt_173_p3, relaydt_173_p4, relaydt_173_p3, 1'b0
  // Relay relay_63: pin names not known; wires that end beside it: relaydt_106_p11[1], relay_63_p2
  LED led_123 (.in(CIncrement[3]));
  // RelayDT #(.poles(4)) relaydt_174: pin names not known; wires that end beside it: 1'b1, 1'b0, relaydt_174_p3, 1'b0, 1'b1, relaydt_174_p6, 1'b0, 1'b1, relaydt_174_p9, REG_C[1], 1'b0, 1'b0, 1'b1, relaydt_174_p14
  // RelayDT #(.poles(4)) relaydt_175: pin names not known; wires that end beside it: 1'b1, 1'b0, relaydt_175_p3[0], relaydt_174_p6, relaydt_174_p3, relaydt_175_p6[0], relaydt_174_p9, 1'b1, relaydt_175_p9[0], REG_B[1], 1'b0, 1'b0, relaydt_174_p14, relaydt_175_p14[0]
  LED led_124 (.in(relaydt_175_p9[0]));
  // RelayDT relaydt_176: pin names not known; wires that end beside it: relaydt_162_p4, 1'b1, 1'b0
  // RelayDT relaydt_177: pin names not known; wires that end beside it: relaydt_162_p5, 1'b0, 1'b1, relaydt_177_p4, relaydt_177_p4, relaydt_177_p6
  // RelayDT relaydt_178: pin names not known; wires that end beside it: relaydt_163_p4, 1'b1, 1'b0
  // RelayDT relaydt_179: pin names not known; wires that end beside it: relaydt_163_p5, 1'b0, 1'b1, relaydt_179_p4, relaydt_179_p4, relaydt_179_p6
  // RelayDT relaydt_180: pin names not known; wires that end beside it: REG_B[0], 1'b0, relaydt_168_p6, REG_B[0], 1'b0, ZERO, 1'b0
  // RelayDT relaydt_181: pin names not known; wires that end beside it: 1'b1, relay_63_p2, relaydt_167_p15, 1'b0
  // RelayDT #(.poles(2)) relaydt_182: pin names not known; wires that end beside it: relay_63_p2, CIncrement[3], relaydt_173_p4, 1'b1, 1'b0
  LED led_125 (.in(relaydt_175_p14[0]));
  // RelayDT #(.poles(4)) relaydt_183: pin names not known; wires that end beside it: relaydt_183_p1, REG_C[2], relaydt_183_p1, relaydt_183_p4, relaydt_183_p5, 1'b0, relaydt_183_p7, relaydt_183_p8, relaydt_177_p6, relaydt_183_p10, relaydt_183_p10, relaydt_183_p7, relaydt_183_p8
  // RelayDT #(.poles(4)) relaydt_184: pin names not known; wires that end beside it: relaydt_184_p1, _1[2], relaydt_184_p1, relaydt_184_p4, relaydt_184_p5, 1'b0, relaydt_184_p7, relaydt_184_p8, relaydt_179_p6, relaydt_184_p10, relaydt_184_p10, relaydt_184_p7, relaydt_184_p8
  // Relay #(.Bits(8)) relay_64: pin names not known; wires that end beside it: in_25, {relaydt_137_p1, relaydt_146_p1[0], relaydt_153_p1[0], relaydt_165_p1[0], relaydt_169_p1[0], relaydt_172_p1[0], relaydt_123_p1[0]}, 1'b0, BUS
  // Relay relay_65: pin names not known; wires that end beside it: relaydt_167_p15, relaydt_106_p11[0], 1'b0, relay_65_p4
  LED led_126 (.in(relaydt_187_p6[0]));
  LED led_127 (.in(relaydt_187_p3[0]));
  // Relay #(.Bits(8)) relay_66: pin names not known; wires that end beside it: in_18, {relaydt_82_p3, relaydt_95_p14[0], relaydt_109_p14[0], relaydt_127_p14[0], relaydt_145_p14[0], relaydt_161_p14[0], relaydt_175_p14[0]}, BUS
  // RelayDT #(.poles(2)) relaydt_185: pin names not known; wires that end beside it: relay_65_p4, relay_65_p4, CIncrement[2], 1'b0, relaydt_173_p4, 1'b1, 1'b0
  LED led_128 (.in(CIncrement[2]));
  // RelayDT #(.poles(4)) relaydt_186: pin names not known; wires that end beside it: 1'b1, 1'b0, relaydt_186_p3, 1'b0, 1'b1, relaydt_186_p6, 1'b0, 1'b1, relaydt_186_p9, REG_C[0], 1'b0
  // RelayDT #(.poles(4)) relaydt_187: pin names not known; wires that end beside it: 1'b1, 1'b0, relaydt_187_p3[0], relaydt_186_p6, relaydt_186_p3, relaydt_187_p6[0], relaydt_186_p9, 1'b0, 1'b1, relaydt_187_p10[0], REG_B[0], 1'b0, in_19, 1'b0
  LED led_129 (.in(relaydt_187_p10[0]));
  // RelayDT relaydt_188: pin names not known; wires that end beside it: relaydt_183_p4, 1'b1, 1'b0
  // RelayDT relaydt_189: pin names not known; wires that end beside it: relaydt_183_p5, 1'b0, 1'b1, relaydt_189_p4, relaydt_189_p4, relaydt_189_p6
  // RelayDT #(.poles(4)) relaydt_190: pin names not known; wires that end beside it: relaydt_190_p1, relaydt_190_p2, relaydt_177_p6, relaydt_183_p10, relaydt_183_p8, relaydt_190_p1, relaydt_190_p1, relaydt_190_p2, 1'b0, relaydt_183_p4, relaydt_190_p11[0], 1'b1, relaydt_183_p5, REG_B[2], 1'b0
  LED led_130 (.in(relaydt_190_p11[0]));
  // RelayDT relaydt_191: pin names not known; wires that end beside it: relaydt_184_p4, 1'b1, 1'b0
  // RelayDT relaydt_192: pin names not known; wires that end beside it: relaydt_184_p5, 1'b0, 1'b1, relaydt_192_p4, relaydt_192_p4, relaydt_192_p6
  // RelayDT #(.poles(4)) relaydt_193: pin names not known; wires that end beside it: relaydt_193_p1, relaydt_193_p2, relaydt_179_p6, relaydt_184_p10, relaydt_184_p8, relaydt_193_p1, relaydt_193_p1, relaydt_193_p2, 1'b0, relaydt_184_p4, relaydt_193_p11[0], 1'b1, relaydt_184_p5, REG_B[2], 1'b0
  LED led_131 (.in(relaydt_193_p11[0]));
  // Relay #(.Bits(8)) relay_67: pin names not known; wires that end beside it: {relaydt_82_p12, relaydt_109_p9[0], relaydt_127_p9[0], relaydt_145_p9[0], relaydt_161_p9[0], relaydt_175_p9[0], relaydt_187_p10[0]}, in_20, BUS, 1'b0
  // Relay #(.Bits(8)) relay_68: pin names not known; wires that end beside it: {relaydt_82_p9, relaydt_109_p6[0], relaydt_127_p6[0], relaydt_145_p6[0], relaydt_161_p6[0], relaydt_175_p6[0], relaydt_187_p6[0]}, in_21, BUS, 1'b0
  // Relay #(.Bits(8)) relay_69: pin names not known; wires that end beside it: {relaydt_82_p6, relaydt_109_p3[0], relaydt_127_p3[0], relaydt_145_p3[0], relaydt_161_p3[0], relaydt_175_p3[0], relaydt_187_p3[0]}, BUS
  // RelayDT #(.poles(4)) relaydt_194: pin names not known; wires that end beside it: relaydt_194_p1, REG_C[1], relaydt_194_p1, relaydt_194_p4, relaydt_194_p5, 1'b0, relaydt_194_p7, relaydt_194_p8, relaydt_189_p6, relaydt_194_p10, relaydt_194_p10, relaydt_194_p7, relaydt_194_p8
  // RelayDT #(.poles(4)) relaydt_195: pin names not known; wires that end beside it: relaydt_195_p1, _1[1], relaydt_195_p1, relaydt_195_p4, relaydt_195_p5, 1'b0, relaydt_195_p7, relaydt_195_p8, relaydt_192_p6, relaydt_195_p10, relaydt_195_p10, relaydt_195_p7, relaydt_195_p8
  // RelayDT #(.poles(4)) relaydt_196: pin names not known; wires that end beside it: in_26[2], 1'b1, 1'b0, 1'b1, 1'b0, 1'b0, 1'b1, 1'b0, 1'b1, 1'b0, relaydt_196_p11, relaydt_196_p12, relaydt_196_p13, relaydt_196_p14, in_26[1], relaydt_196_p11, 1'b0, 1'b0, relaydt_196_p12, relaydt_196_p13, 1'b0, 1'b0, relaydt_196_p14
  // Relay relay_70: pin names not known; wires that end beside it: relaydt_167_p15, relaydt_143_p11[0], 1'b0, relay_70_p4
  LED led_132 (.in(CIncrement[1]));
  // RelayDT #(.poles(4)) relaydt_197: pin names not known; wires that end beside it: 1'b0, in_26[0]
  // RelayDT #(.poles(2)) relaydt_198: pin names not known; wires that end beside it: relay_70_p4, relay_70_p4, CIncrement[1], 1'b0, relaydt_173_p4, 1'b1, 1'b0
  // RelayDT #(.poles(4)) relaydt_199: pin names not known; wires that end beside it: relaydt_199_p1, relaydt_199_p2, relaydt_189_p6, relaydt_194_p10, relaydt_194_p8, relaydt_199_p1, relaydt_199_p1, relaydt_199_p2, 1'b0, relaydt_194_p4, relaydt_199_p11[0], 1'b1, relaydt_194_p5, REG_B[1], 1'b0
  // RelayDT #(.poles(4)) relaydt_200: pin names not known; wires that end beside it: relaydt_200_p1, relaydt_200_p2, relaydt_192_p6, relaydt_195_p10, relaydt_195_p8, relaydt_200_p1, relaydt_200_p1, relaydt_200_p2, 1'b0, relaydt_195_p4, relaydt_200_p11[0], 1'b1, relaydt_195_p5, REG_B[1], 1'b0
  // RelayDT #(.poles(8)) relaydt_201: pin names not known; wires that end beside it: relaydt_201_p1, 1'b0, 1'b0, relaydt_201_p1, relaydt_201_p5, 1'b0, 1'b0, relaydt_201_p5, relaydt_201_p9, 1'b0, 1'b0, relaydt_201_p9, relaydt_201_p13, 1'b0, 1'b0, relaydt_201_p13, 1'b0, in_25, in_21, in_20, in_19, in_18, in_24, in_22, relaydt_201_p25
  // Relay relay_71: pin names not known; wires that end beside it: relaydt_167_p15, relaydt_167_p11[0], 1'b0, relay_71_p4
  // RelayDT relaydt_202: pin names not known; wires that end beside it: relaydt_194_p4, 1'b1, 1'b0
  // RelayDT relaydt_203: pin names not known; wires that end beside it: relaydt_194_p5, 1'b0, 1'b1, relaydt_203_p4, relaydt_203_p4, relaydt_203_p6
  LED led_133 (.in(relaydt_199_p11[0]));
  // RelayDT relaydt_204: pin names not known; wires that end beside it: relaydt_195_p4, 1'b1, 1'b0
  // RelayDT relaydt_205: pin names not known; wires that end beside it: relaydt_195_p5, 1'b0, 1'b1, relaydt_205_p4, relaydt_205_p4, relaydt_205_p6
  LED led_134 (.in(relaydt_200_p11[0]));
  LED led_135 (.in(in_25));
  LED led_136 (.in(in_21));
  LED led_137 (.in(in_20));
  LED led_138 (.in(in_19));
  LED led_139 (.in(in_18));
  LED led_140 (.in(in_24));
  LED led_141 (.in(in_22));
  LED led_142 (.in(relaydt_201_p25));
  // RelayDT #(.poles(2)) relaydt_206: pin names not known; wires that end beside it: relay_71_p4, relay_71_p4, CIncrement[0], 1'b0, relaydt_173_p4, 1'b1, 1'b0
  LED led_143 (.in(CIncrement[0]));
  // RelayDT #(.poles(4)) relaydt_207: pin names not known; wires that end beside it: relaydt_207_p1, REG_C[0], relaydt_207_p1, 1'b0, relaydt_207_p5, relaydt_207_p6, relaydt_203_p6, relaydt_207_p8, relaydt_207_p8, relaydt_207_p5, relaydt_207_p6
  // RelayDT #(.poles(4)) relaydt_208: pin names not known; wires that end beside it: relaydt_208_p1, _1[0], relaydt_208_p1, 1'b0, relaydt_208_p5, relaydt_208_p6, relaydt_205_p6, relaydt_208_p8, relaydt_208_p8, relaydt_208_p5, relaydt_208_p6
  // RelayDT #(.poles(4)) relaydt_209: pin names not known; wires that end beside it: relaydt_209_p1, relaydt_209_p2, relaydt_203_p6, relaydt_207_p8, relaydt_207_p6, relaydt_209_p1, relaydt_209_p1, relaydt_209_p2, 1'b0, 1'b1, relaydt_209_p11[0], 1'b1, 1'b0, REG_B[0], in_22, 1'b0
  // RelayDT #(.poles(4)) relaydt_210: pin names not known; wires that end beside it: relaydt_210_p1, relaydt_210_p2, relaydt_205_p6, relaydt_208_p8, relaydt_208_p6, relaydt_210_p1, relaydt_210_p1, relaydt_210_p2, 1'b0, 1'b1, relaydt_210_p11[0], 1'b1, 1'b0, REG_B[0], in_24, 1'b0
  // Relay #(.Bits(8)) relay_72: pin names not known; wires that end beside it: {relaydt_91_p11, relaydt_128_p11[0], relaydt_150_p11[0], relaydt_170_p11[0], relaydt_190_p11[0], relaydt_199_p11[0], relaydt_209_p11[0]}, BUS
  LED led_144 (.in(relaydt_209_p11[0]));
  // Relay #(.Bits(8)) relay_73: pin names not known; wires that end beside it: {relaydt_92_p11, relaydt_129_p11[0], relaydt_151_p11[0], relaydt_171_p11[0], relaydt_193_p11[0], relaydt_200_p11[0], relaydt_210_p11[0]}, BUS
  LED led_145 (.in(relaydt_210_p11[0]));

  // Other names for the same wires on the sheet: REG_B[7] = B_SIGN; AND_E = in_18; INCB_E = in_24; NOTB_E = in_21;
  //   OR_E = in_19; RESET = in_28; RSC = in_17; SHLB_E = in_25; SUM_E = in_22; XOR_E = in_20

  // Notes on the sheet:
  //   clk: Hz: 4
  //   clk_2: Hz: 8
  //   clk_3: Hz: 16
  //   clk_4: Hz: 2
  //   MANUAL: default 1
  //   _1: default 1
  //   _1_2: default 1
  //   _1_3: default 1
  //   CLOCK
  //   B Register
  //   C Register
  //   Inst Register
  //   Mem Address Register
  //   Output Register
  //   uCounter
  //   ALU-Logic
  //   AND
  //   ALU-Arithmetic
  //   SCZ Register
  //   Counter
  //   XOR
  //   NOT_B
  //   OR
  //   SUM
  //   contents of R1 (hex, n*v repeats v):
  //   4004,1408,6*0,4004,1408,4800,1200,4*0,4004,1408,4800,1020,281
  //   ,0,0,0,4004,1408,4800,1020,2c1,0,0,0,4004,1408,4800,2100,4*0,4004
  //   ,1408,a00,5*0,4004,1408,802,5*0,4004,1408,6*0,4004,1408,46*0,4004
  //   ,1408,110,5*0,4004,1408,8000,5*0,4004,1408,6*0,4004,1408,4800
  //   ,1200,4*0,4004,1408,4800,1020,281,0,0,0,4004,1408,4800,1020,2c1
  //   ,0,0,0,4004,1408,4800,2100,4*0,4004,1408,a00,5*0,4004,1408,802
  //   ,5*0,4004,1408,802,5*0,4004,1408,46*0,4004,1408,110,5*0,4004,1408
  //   ,8000,5*0,4004,1408,6*0,4004,1408,4800,1200,4*0,4004,1408,4800
  //   ,1020,281,0,0,0,4004,1408,4800,1020,2c1,0,0,0,4004,1408,4800,2100
  //   ,4*0,4004,1408,a00,5*0,4004,1408,802,5*0,4004,1408,6*0,4004,1408
  //   ,802,45*0,4004,1408,110,5*0,4004,1408,8000,5*0,4004,1408,6*0,4004
  //   ,1408,4800,1200,4*0,4004,1408,4800,1020,281,0,0,0,4004,1408,4800
  //   ,1020,2c1,0,0,0,4004,1408,4800,2100,4*0,4004,1408,a00,5*0,4004
  //   ,1408,802,5*0,4004,1408,802,5*0,4004,1408,802,45*0,4004,1408,110
  //   ,5*0,4004,1408,8000
  //   SHL
  //   3-8 Decoder - no Z
endmodule
