// Digital circuit controlled_output.dig as structural Verilog
module controlled_output (
  input  [5:0] SRC,
  input  [5:0] REG,
  input  [7:0] VAL,
  output [7:0] OUT,
  output TRG
);

  Comparator #(.Bits(6)) comparator_1 (.a(SRC), .b(REG), .eq(TRG));  // open: gt, lt
  assign OUT = TRG ? VAL : 8'bz;  // Driver driver_1
endmodule
