// Digital circuit controlled_register.dig as structural Verilog
module controlled_register (
  input  [7:0] IN,
  input  [5:0] SRC,
  input  [5:0] REG,
  input  [5:0] DST,
  input  CLK,
  input  RST,
  output [7:0] VAL,
  output [7:0] OUT
);

  wire comparator_1_eq, comparator_2_eq, or_1_out;
  wire [7:0] multiplexer_1_out;

  Comparator #(.Bits(6)) comparator_1 (.a(SRC), .b(REG), .eq(comparator_1_eq));  // open: gt, lt
  Comparator #(.Bits(6)) comparator_2 (.a(DST), .b(REG), .eq(comparator_2_eq));  // open: gt, lt
  Multiplexer #(.Bits(8)) multiplexer_1 (.sel(RST), .in_0(IN), .in_1({8{1'b0}}), .out(multiplexer_1_out));
  or or_1 (or_1_out, RST, comparator_2_eq);
  Register #(.Bits(8)) Register (.D(multiplexer_1_out), .C(CLK), .en(or_1_out), .Q(VAL));
  assign OUT = comparator_1_eq ? VAL : 8'bz;  // Driver driver_1
endmodule
