// Digital circuit risc_like_8bit_digital.dig as structural Verilog
module risc_like_8bit_digital (
  input  clk,
  input  HALT,
  input  in_3,
  input  clk_2,
  input  clk_3,
  input  in_6,
  input  clk_4,
  input  MANUAL,
  input  [7:0] in_9,
  input  Manual_Load_BUS,
  input  in_11,
  input  in_12
);

  wire ADD_C, ADD_C_p8, and_1_out, and_2_out, and_3_out, BI1, CLK_A, CLK_B, CLOCK, comparator_1_eq,
       comparator_2_eq, comparator_3_eq, comparator_4_eq, decoder_1_out_0, decoder_1_out_1, delay_1_out,
       delay_2_out, GTJ, HALT_t, nCLOCK, or_1_out, or_3_out, or_4_out, or_5_out, or_6_out, relaydt_1_p7,
       relaydt_1_p8, relaydt_2_p2, rs_ff_1_nq, rs_ff_1_q, STEP_out;
  wire [0:0] ADD_C_p2;
  wire [1:0] counter_1_out;
  wire [3:0] binary_to_bcd_1__1s, binary_to_bcd_1__10s, binary_to_bcd_1__100s, binary_to_bcd_2__1s,
       binary_to_bcd_2__10s, binary_to_bcd_2__100s, binary_to_bcd_3__1s, binary_to_bcd_3__10s,
       binary_to_bcd_3__100s;
  wire [5:0] DEST, SOURCE;
  wire [7:0] ADD_1_p9, add_1_s, ADD_2_p9, add_3_s, BI1_p9, BUS, JUMP, multiplexer_1_out, multiplexer_2_out,
       multiplexer_3_out, multiplexer_4_out, multiplexer_5_out, Output_Register_q, PC, PC_INC_q, REG_A_2_p9,
       REG_A_p9, REG_B_p9;
  wire [7:1] GTJ_p9;
  wire [15:6] eepromdualport_1_d;

  // RelayDT #(.poles(2)) relaydt_1: pin names not known; wires that end beside it: in_6, clk_3, clk_2, clk, clk_4, 1'b0, relaydt_1_p7, relaydt_1_p8, in_3, relaydt_1_p7, relaydt_1_p8
  or or_1 (or_1_out, HALT, HALT_t);
  EEPROMDualPort #(.AddrBits(8), .isProgramMemory("true"), .Bits(16)) eepromdualport_1 (
    .A(PC), .Din({16{1'b0}}), .str(1'b0), .C(CLOCK), .ld(1'b1), .D({eepromdualport_1_d, DEST}));
  // RelayDT relaydt_2: pin names not known; wires that end beside it: 1'b0, relaydt_2_p2
  Button STEP (.out(STEP_out));
  and and_1 (and_1_out, STEP_out, MANUAL, ~or_1_out);  // And
  RS_FF rs_ff_1 (.S(and_2_out), .C(relaydt_2_p2), .R(~and_2_out), .Q(rs_ff_1_q), .nQ(rs_ff_1_nq));
  Decoder #(.Selector_Bits(2)) decoder_1 (
    .sel(eepromdualport_1_d[15:14]), .out_0(decoder_1_out_0), .out_1(decoder_1_out_1), .out_3(HALT_t));  // open: out_2
  and and_2 (and_2_out, ~MANUAL, ~or_1_out, rs_ff_1_nq);  // And
  or or_2 (CLOCK, and_1_out, rs_ff_1_q);
  assign SOURCE = decoder_1_out_0 ? eepromdualport_1_d[11:6] : 6'bz;  // Driver driver_1
  assign BUS = decoder_1_out_1 ? eepromdualport_1_d[13:6] : 8'bz;  // Driver driver_2
  not not_1 (nCLOCK, CLOCK);
  Counter #(.Bits(2)) counter_1 (.en(1'b1), .C(CLOCK), .clr(and_2_out), .out(counter_1_out));  // open: ovf
  LED led_1 (.in(CLOCK));
  LED led_2 (.in(nCLOCK));
  LED led_3 (.in(BUS[7]));
  Decoder #(.Selector_Bits(2)) decoder_2 (.sel(counter_1_out), .out_1(CLK_A), .out_3(CLK_B));  // open: out_0, out_2
  LED led_4 (.in(BUS[5]));
  LED led_5 (.in(BUS[6]));
  LED led_6 (.in(CLK_A));
  LED led_7 (.in(CLK_B));
  LED led_8 (.in(BUS[3]));
  LED led_9 (.in(BUS[4]));
  assign BUS = Manual_Load_BUS ? in_9 : 8'bz;  // Driver driver_3
  LED led_10 (.in(BUS[1]));
  LED led_11 (.in(BUS[2]));
  LED led_12 (.in(BUS[0]));
  or or_3 (or_3_out, BI1, GTJ);
  Comparator #(.Bits(6)) comparator_1 (.a(SOURCE), .b(6'b000010), .eq(comparator_1_eq));  // open: gt, lt
  Comparator #(.Bits(6)) comparator_2 (.a(DEST), .b(6'b000010), .eq(comparator_2_eq));  // open: gt, lt
  Multiplexer #(.Bits(8)) multiplexer_1 (.sel(in_11), .in_0(BUS), .in_1({8{1'b0}}), .out(multiplexer_1_out));
  or or_4 (or_4_out, in_11, CLK_B, comparator_2_eq);
  or or_5 (or_5_out, CLK_B, CLK_A);
  Register #(.Bits(8)) Output_Register (.D(BUS), .C(CLOCK), .en(in_12), .Q(Output_Register_q));
  and and_3 (and_3_out, or_3_out, DEST[5]);
  Multiplexer #(.Bits(8)) multiplexer_2 (
    .sel(CLK_B), .in_0(multiplexer_1_out), .in_1(multiplexer_3_out), .out(multiplexer_2_out));
  // controlled_register REG_A: pin names not known; wires that end beside it: BUS, {8{1'b0}}, SOURCE, 6'b000011, DEST, CLK_A, in_11, 1'b0, REG_A_p9, BUS
  // controlled_register ADD_1: pin names not known; wires that end beside it: BUS, {8{1'b0}}, SOURCE, 6'b001111, DEST, CLK_A, in_11, 1'b0, ADD_1_p9
  // controlled_register ADD_2: pin names not known; wires that end beside it: BUS, {8{1'b0}}, SOURCE, 6'b010000, DEST, CLK_A, in_11, 1'b0, ADD_2_p9
  // controlled_register ADD_C: pin names not known; wires that end beside it: BUS, {{7{1'b0}}, ADD_C_p2[0]}, SOURCE, 6'b010001, DEST, CLK_A, in_11, ADD_C_p8, ADD_C, BUS
  Binary_to_BCD binary_to_bcd_1 (
    .In(Output_Register_q), ._100s(binary_to_bcd_1__100s), ._10s(binary_to_bcd_1__10s),
    ._1s(binary_to_bcd_1__1s));
  Seven_Seg_Hex seven_seg_hex_1 (.d(binary_to_bcd_1__100s), .dp(1'b0));
  Register #(.Bits(8)) Program_Counter (.D(multiplexer_2_out), .C(or_5_out), .en(or_4_out), .Q(PC));
  LED led_13 (.in(PC[7]));
  Binary_to_BCD binary_to_bcd_2 (
    .In(REG_A_p9), ._100s(binary_to_bcd_2__100s), ._10s(binary_to_bcd_2__10s), ._1s(binary_to_bcd_2__1s));
  LED led_14 (.in(REG_A_p9[7]));
  LED led_15 (.in(REG_A_p9[6]));
  LED led_16 (.in(REG_A_p9[5]));
  LED led_17 (.in(REG_A_p9[4]));
  Seven_Seg_Hex seven_seg_hex_2 (.d(binary_to_bcd_1__10s), .dp(1'b0));
  Seven_Seg_Hex seven_seg_hex_3 (.d(binary_to_bcd_1__1s), .dp(1'b0));
  Multiplexer #(.Bits(8)) multiplexer_3 (.sel(and_3_out), .in_0(PC_INC_q), .in_1(JUMP), .out(multiplexer_3_out));
  Driver #(.Bits(8)) driver_4 (.in(PC), .en(comparator_1_eq));  // open: out
  LED led_18 (.in(PC[6]));
  LED led_19 (.in(PC[5]));
  LED led_20 (.in(PC[4]));
  LED led_21 (.in(PC[3]));
  Seven_Seg_Hex seven_seg_hex_4 (.d(binary_to_bcd_2__100s), .dp(1'b0));
  LED led_22 (.in(REG_A_p9[3]));
  LED led_23 (.in(REG_A_p9[2]));
  LED led_24 (.in(REG_A_p9[1]));
  LED led_25 (.in(REG_A_p9[0]));
  Add #(.Bits(8)) add_1_dup2 (.a(ADD_1_p9), .b(ADD_2_p9), .c_i(1'b0), .s(add_1_s), .c_o(ADD_C_p2[0]));
  LED led_26 (.in(PC[2]));
  LED led_27 (.in(PC[1]));
  LED led_28 (.in(PC[0]));
  Seven_Seg_Hex seven_seg_hex_5 (.d(binary_to_bcd_2__10s), .dp(1'b0));
  Seven_Seg_Hex seven_seg_hex_6 (.d(binary_to_bcd_2__1s), .dp(1'b0));
  // controlled_output ADD_2: pin names not known; wires that end beside it: SOURCE, 6'b010000, add_1_s, BUS, ADD_C_p8
  Add #(.Bits(8)) add_3 (.a(PC), .b({8{1'b0}}), .c_i(1'b1), .s(add_3_s));  // open: c_o
  Comparator #(.Bits(6)) comparator_3 (.a(SOURCE), .b(6'b100001), .eq(comparator_3_eq));  // open: gt, lt
  Comparator #(.Bits(6)) comparator_4 (.a(DEST), .b(6'b100001), .eq(comparator_4_eq));  // open: gt, lt
  Delay #(.delayTime(2)) delay_1 (.in(CLK_A), .out(delay_1_out));
  Multiplexer #(.Bits(8)) multiplexer_4 (.sel(comparator_4_eq), .in_0(add_3_s), .in_1(BUS), .out(multiplexer_4_out));
  // controlled_register REG_A_2: pin names not known; wires that end beside it: BUS, add_3_s, SOURCE, 6'b100001, DEST, delay_1_out, in_11, CLK_A, REG_A_2_p9
  // controlled_register REG_B: pin names not known; wires that end beside it: BUS, {8{1'b0}}, SOURCE, 6'b000100, DEST, CLK_A, in_11, 1'b0, REG_B_p9, BUS
  // controlled_register JUMP: pin names not known; wires that end beside it: BUS, {8{1'b0}}, SOURCE, 6'b100000, DEST, CLK_A, in_11, 1'b0, JUMP
  // controlled_register BI1: pin names not known; wires that end beside it: BUS, {8{1'b0}}, SOURCE, 6'b100100, DEST, CLK_A, in_11, 1'b0, BI1_p9
  // controlled_register GTJ: pin names not known; wires that end beside it: BUS, {8{1'b0}}, SOURCE, 6'b110001, DEST, CLK_A, in_11, 1'b0, {GTJ_p9, GTJ}
  Multiplexer #(.Bits(8)) multiplexer_5 (
    .sel(in_11), .in_0(multiplexer_4_out), .in_1({8{1'b0}}), .out(multiplexer_5_out));
  or or_6 (or_6_out, in_11, CLK_A, comparator_4_eq);
  Delay #(.delayTime(2)) delay_2 (.in(CLK_A), .out(delay_2_out));
  LED led_29 (.in(REG_A_2_p9[7]));
  LED led_30 (.in(REG_A_2_p9[6]));
  Register #(.Bits(8)) PC_INC (.D(multiplexer_5_out), .C(delay_2_out), .en(or_6_out), .Q(PC_INC_q));
  LED led_31 (.in(REG_A_2_p9[5]));
  LED led_32 (.in(REG_A_2_p9[4]));
  LED led_33 (.in(REG_A_2_p9[3]));
  LED led_34 (.in(REG_A_2_p9[2]));
  Binary_to_BCD binary_to_bcd_3 (
    .In(REG_B_p9), ._100s(binary_to_bcd_3__100s), ._10s(binary_to_bcd_3__10s), ._1s(binary_to_bcd_3__1s));
  Comparator #(.Bits(8)) comparator_5 (.a(8'h1), .b(BI1_p9), .eq(BI1));  // open: gt, lt
  Driver #(.Bits(8)) driver_5 (.in(PC_INC_q), .en(comparator_3_eq));  // open: out
  LED led_35 (.in(REG_A_2_p9[1]));
  LED led_36 (.in(REG_A_2_p9[0]));
  Seven_Seg_Hex seven_seg_hex_7 (.d(binary_to_bcd_3__100s), .dp(1'b0));
  Seven_Seg_Hex seven_seg_hex_8 (.d(binary_to_bcd_3__10s), .dp(1'b0));
  Seven_Seg_Hex seven_seg_hex_9 (.d(binary_to_bcd_3__1s), .dp(1'b0));

  // Other names for the same wires on the sheet: RESET = in_11

  // Notes on the sheet:
  //   clk: Hz: 8
  //   clk_2: Hz: 16
  //   clk_3: Hz: 64
  //   clk_4: Hz: 2
  //   MANUAL: default 1
  //   CLOCK
  //   contents of eepromdualport_1 (hex, n*v repeats v):
  //   6043,4804,110,4031,cf,403,43e0,464,40e0,4071,5*0,c000
endmodule
