// Digital circuit risc_like_8bit_relay.dig as structural Verilog
module risc_like_8bit_relay (
  input  in_1,
  input  in_2,
  input  in_3,
  input  in_4,
  input  in_5,
  input  in_6,
  input  in_7,
  input  in_8,
  input  [5:0] LOAD,
  input  [5:0] SELECT
);

  wire B_0, B_1, B_2, B_3, B_4, B_5, B_6, B_7, diodebackward_1_out, diodebackward_2_out, diodebackward_3_out,
       diodebackward_4_out, relaydt_1_p3, relaydt_2_p3, relaydt_3_p3, relaydt_4_p3, relaydt_5_p2,
       relaydt_6_p2, relaydt_7_p2, relaydt_8_p2, relaydt_9_p2, relaydt_10_p2, relaydt_11_p2, relaydt_12_p2,
       relaydt_13_p2, relaydt_14_p2, relaydt_15_p2, relaydt_16_p2, relaydt_17_p2, relaydt_18_p2,
       relaydt_19_p2, relaydt_20_p2, relaydt_21_p2, relaydt_22_p2, relaydt_23_p2, relaydt_24_p2,
       relaydt_25_p3, relaydt_25_p4, relaydt_26_p1, relaydt_26_p4, relaydt_26_p7, relaydt_27_p3,
       relaydt_27_p4, relaydt_28_p1, relaydt_28_p4, relaydt_28_p7, relaydt_29_p4, relaydt_30_p5,
       relaydt_31_p3, relaydt_32_p5, relaydt_33_p6, relaydt_34_p5, relaydt_35_p6, relaydt_35_p9,
       relaydt_36_p5, relaydt_37_p6, relaydt_37_p9, relaydt_38_p5, relaydt_39_p5, relaydt_40_p5,
       relaydt_41_p6, relaydt_41_p9, relaydt_42_p6, relaydt_42_p9, relaydt_43_p5, relaydt_44_p5,
       relaydt_45_p5, relaydt_46_p5, relaydt_47_p6, relaydt_47_p9, relaydt_48_p5, relaydt_49_p6,
       relaydt_49_p9, relaydt_50_p5, relaydt_51_p5, relaydt_52_p5;
  wire [5:0] not_1_out, not_2_out;

  assign not_1_out = ~6'b000010;  // Not not_1, 6 bits wide
  assign not_2_out = ~6'b000011;  // Not not_2, 6 bits wide
  // RelayDT relaydt_1: pin names not known; wires that end beside it: SELECT[5], 1'b0, relaydt_1_p3, SELECT[4]
  DiodeBackward diodebackward_1 (.in(relaydt_1_p3), .out(diodebackward_1_out));
  PullUp pullup_1 (.out(diodebackward_1_out));
  LED led_1 (.in(diodebackward_1_out));
  // RelayDT relaydt_2: pin names not known; wires that end beside it: LOAD[5], 1'b0, relaydt_2_p3, LOAD[4]
  DiodeBackward diodebackward_2 (.in(relaydt_2_p3), .out(diodebackward_2_out));
  PullUp pullup_2 (.out(diodebackward_2_out));
  LED led_2 (.in(diodebackward_2_out));
  // RelayDT relaydt_3: pin names not known; wires that end beside it: SELECT[5], 1'b0, relaydt_3_p3, SELECT[4]
  DiodeBackward diodebackward_3 (.in(relaydt_3_p3), .out(diodebackward_3_out));
  PullUp pullup_3 (.out(diodebackward_3_out));
  LED led_3 (.in(diodebackward_3_out));
  // RelayDT relaydt_4: pin names not known; wires that end beside it: LOAD[5], 1'b0, relaydt_4_p3, LOAD[4]
  DiodeBackward diodebackward_4 (.in(relaydt_4_p3), .out(diodebackward_4_out));
  PullUp pullup_4 (.out(diodebackward_4_out));
  LED led_4 (.in(diodebackward_4_out));
  // RelayDT relaydt_5: pin names not known; wires that end beside it: 1'b0, relaydt_5_p2, SELECT[3]
  DiodeBackward diodebackward_5 (.in(relaydt_5_p2), .out(diodebackward_1_out));
  // RelayDT relaydt_6: pin names not known; wires that end beside it: 1'b0, relaydt_6_p2, LOAD[3]
  DiodeBackward diodebackward_6 (.in(relaydt_6_p2), .out(diodebackward_2_out));
  // RelayDT relaydt_7: pin names not known; wires that end beside it: 1'b0, relaydt_7_p2, SELECT[3]
  DiodeBackward diodebackward_7 (.in(relaydt_7_p2), .out(diodebackward_3_out));
  // RelayDT relaydt_8: pin names not known; wires that end beside it: 1'b0, relaydt_8_p2, LOAD[3]
  DiodeBackward diodebackward_8 (.in(relaydt_8_p2), .out(diodebackward_4_out));
  // RelayDT relaydt_9: pin names not known; wires that end beside it: 1'b0, relaydt_9_p2, SELECT[2]
  DiodeBackward diodebackward_9 (.in(relaydt_9_p2), .out(diodebackward_1_out));
  // RelayDT relaydt_10: pin names not known; wires that end beside it: 1'b0, relaydt_10_p2, LOAD[2]
  DiodeBackward diodebackward_10 (.in(relaydt_10_p2), .out(diodebackward_2_out));
  // RelayDT relaydt_11: pin names not known; wires that end beside it: 1'b0, relaydt_11_p2, SELECT[2]
  DiodeBackward diodebackward_11 (.in(relaydt_11_p2), .out(diodebackward_3_out));
  // RelayDT relaydt_12: pin names not known; wires that end beside it: 1'b0, relaydt_12_p2, LOAD[2]
  DiodeBackward diodebackward_12 (.in(relaydt_12_p2), .out(diodebackward_4_out));
  // RelayDT relaydt_13: pin names not known; wires that end beside it: 1'b0, relaydt_13_p2, SELECT[1]
  DiodeBackward diodebackward_13 (.in(relaydt_13_p2), .out(diodebackward_1_out));
  // RelayDT relaydt_14: pin names not known; wires that end beside it: 1'b0, relaydt_14_p2, LOAD[1]
  DiodeBackward diodebackward_14 (.in(relaydt_14_p2), .out(diodebackward_2_out));
  // RelayDT relaydt_15: pin names not known; wires that end beside it: 1'b0, relaydt_15_p2, SELECT[1]
  DiodeBackward diodebackward_15 (.in(relaydt_15_p2), .out(diodebackward_3_out));
  // RelayDT relaydt_16: pin names not known; wires that end beside it: 1'b0, relaydt_16_p2, LOAD[1]
  DiodeBackward diodebackward_16 (.in(relaydt_16_p2), .out(diodebackward_4_out));
  // RelayDT relaydt_17: pin names not known; wires that end beside it: 1'b0, relaydt_17_p2, SELECT[0]
  DiodeBackward diodebackward_17 (.in(relaydt_17_p2), .out(diodebackward_1_out));
  // RelayDT relaydt_18: pin names not known; wires that end beside it: 1'b0, relaydt_18_p2, LOAD[0]
  DiodeBackward diodebackward_18 (.in(relaydt_18_p2), .out(diodebackward_2_out));
  // RelayDT relaydt_19: pin names not known; wires that end beside it: 1'b0, relaydt_19_p2, SELECT[0]
  DiodeBackward diodebackward_19 (.in(relaydt_19_p2), .out(diodebackward_3_out));
  // RelayDT relaydt_20: pin names not known; wires that end beside it: 1'b0, relaydt_20_p2, LOAD[0]
  DiodeBackward diodebackward_20 (.in(relaydt_20_p2), .out(diodebackward_4_out));
  DiodeForward diodeforward_1 (.in(in_8), .out(B_7));
  DiodeForward diodeforward_2 (.in(in_7), .out(B_6));
  LED led_5 (.in(B_7));
  PullDown pulldown_1 (.out(B_7));
  PullDown pulldown_2 (.out(B_6));
  // RelayDT relaydt_21: pin names not known; wires that end beside it: 1'b0, relaydt_21_p2, diodebackward_2_out, 1'b0
  DiodeBackward diodebackward_21 (.in(relaydt_21_p2), .out(diodebackward_1_out));
  // RelayDT relaydt_22: pin names not known; wires that end beside it: 1'b0, relaydt_22_p2
  DiodeBackward diodebackward_22 (.in(relaydt_22_p2), .out(diodebackward_2_out));
  // RelayDT relaydt_23: pin names not known; wires that end beside it: 1'b0, relaydt_23_p2, diodebackward_4_out, 1'b0
  DiodeBackward diodebackward_23 (.in(relaydt_23_p2), .out(diodebackward_3_out));
  // RelayDT relaydt_24: pin names not known; wires that end beside it: 1'b0, relaydt_24_p2
  DiodeBackward diodebackward_24 (.in(relaydt_24_p2), .out(diodebackward_4_out));
  DiodeForward diodeforward_3 (.in(in_6), .out(B_5));
  DiodeForward diodeforward_4 (.in(in_5), .out(B_4));
  LED led_6 (.in(B_6));
  LED led_7 (.in(B_5));
  PullDown pulldown_3 (.out(B_5));
  PullDown pulldown_4 (.out(B_4));
  DiodeForward diodeforward_5 (.in(in_4), .out(B_3));
  DiodeForward diodeforward_6 (.in(in_3), .out(B_2));
  LED led_8 (.in(B_4));
  LED led_9 (.in(B_3));
  PullDown pulldown_5 (.out(B_3));
  PullDown pulldown_6 (.out(B_2));
  // RelayDT #(.poles(2)) relaydt_25: pin names not known; wires that end beside it: 1'b1, 1'b1, relaydt_25_p3, relaydt_25_p4
  // RelayDT #(.poles(2)) relaydt_26: pin names not known; wires that end beside it: relaydt_26_p1, 1'b0, B_7, relaydt_26_p4, relaydt_26_p4, B_6, relaydt_26_p7, 1'b0
  // RelayDT #(.poles(2)) relaydt_27: pin names not known; wires that end beside it: 1'b1, 1'b1, relaydt_27_p3, relaydt_27_p4
  // RelayDT #(.poles(2)) relaydt_28: pin names not known; wires that end beside it: relaydt_28_p1, 1'b0, B_7, relaydt_28_p4, relaydt_28_p4, B_6, relaydt_28_p7, 1'b0
  DiodeForward diodeforward_7 (.in(in_2), .out(B_1));
  DiodeForward diodeforward_8 (.in(in_1), .out(B_0));
  LED led_10 (.in(B_2));
  LED led_11 (.in(B_1));
  PullDown pulldown_7 (.out(B_1));
  PullDown pulldown_8 (.out(B_0));
  // RelayDT #(.poles(2)) relaydt_29: pin names not known; wires that end beside it: relaydt_25_p3, 1'b1, 1'b0, relaydt_29_p4
  // RelayDT #(.poles(2)) relaydt_30: pin names not known; wires that end beside it: relaydt_26_p4, 1'b1, relaydt_25_p4, 1'b0, relaydt_30_p5
  LED led_12 (.in(relaydt_30_p5));
  // RelayDT #(.poles(2)) relaydt_31: pin names not known; wires that end beside it: relaydt_27_p3, 1'b1, relaydt_31_p3
  // RelayDT #(.poles(2)) relaydt_32: pin names not known; wires that end beside it: relaydt_28_p4, 1'b1, relaydt_27_p4, 1'b0, relaydt_32_p5
  LED led_13 (.in(relaydt_32_p5));
  LED led_14 (.in(B_0));
  // RelayDT #(.poles(2)) relaydt_33: pin names not known; wires that end beside it: relaydt_26_p7, 1'b1, 1'b0, relaydt_25_p4, 1'b0, relaydt_33_p6
  // RelayDT #(.poles(2)) relaydt_34: pin names not known; wires that end beside it: relaydt_28_p7, 1'b1, relaydt_27_p4, 1'b0, relaydt_34_p5
  DiodeForward diodeforward_9 (.in(diodebackward_1_out), .out(relaydt_26_p1));
  DiodeForward diodeforward_10 (.in(relaydt_29_p4), .out(relaydt_26_p1));
  PullDown pulldown_9 (.out(relaydt_26_p1));
  // RelayDT #(.poles(2)) relaydt_35: pin names not known; wires that end beside it: relaydt_26_p7, relaydt_26_p1, 1'b0, 1'b0, B_5, relaydt_35_p6, relaydt_35_p6, B_4, relaydt_35_p9, 1'b0
  // RelayDT #(.poles(2)) relaydt_36: pin names not known; wires that end beside it: relaydt_35_p6, 1'b1, relaydt_25_p4, 1'b0, relaydt_36_p5
  LED led_15 (.in(relaydt_33_p6));
  DiodeForward diodeforward_11 (.in(diodebackward_3_out), .out(relaydt_28_p1));
  DiodeForward diodeforward_12 (.in(relaydt_31_p3), .out(relaydt_28_p1));
  PullDown pulldown_10 (.out(relaydt_28_p1));
  // RelayDT #(.poles(2)) relaydt_37: pin names not known; wires that end beside it: relaydt_28_p7, relaydt_28_p1, 1'b0, 1'b0, B_5, relaydt_37_p6, relaydt_37_p6, B_4, relaydt_37_p9, 1'b0
  // RelayDT #(.poles(2)) relaydt_38: pin names not known; wires that end beside it: relaydt_37_p6, 1'b1, relaydt_27_p4, 1'b0, relaydt_38_p5
  LED led_16 (.in(relaydt_34_p5));
  // RelayDT #(.poles(2)) relaydt_39: pin names not known; wires that end beside it: relaydt_35_p9, 1'b1, relaydt_25_p4, 1'b0, relaydt_39_p5
  LED led_17 (.in(relaydt_36_p5));
  // RelayDT #(.poles(2)) relaydt_40: pin names not known; wires that end beside it: relaydt_37_p9, 1'b1, relaydt_27_p4, 1'b0, relaydt_40_p5
  LED led_18 (.in(relaydt_38_p5));
  // RelayDT #(.poles(2)) relaydt_41: pin names not known; wires that end beside it: relaydt_35_p9, relaydt_26_p1, 1'b0, 1'b0, B_3, relaydt_41_p6, relaydt_41_p6, B_2, relaydt_41_p9, 1'b0
  LED led_19 (.in(relaydt_39_p5));
  // RelayDT #(.poles(2)) relaydt_42: pin names not known; wires that end beside it: relaydt_37_p9, relaydt_28_p1, 1'b0, 1'b0, B_3, relaydt_42_p6, relaydt_42_p6, B_2, relaydt_42_p9, 1'b0
  LED led_20 (.in(relaydt_40_p5));
  // RelayDT #(.poles(2)) relaydt_43: pin names not known; wires that end beside it: relaydt_41_p6, 1'b1, relaydt_25_p4, 1'b0, relaydt_43_p5
  LED led_21 (.in(relaydt_43_p5));
  // RelayDT #(.poles(2)) relaydt_44: pin names not known; wires that end beside it: relaydt_42_p6, 1'b1, relaydt_27_p4, 1'b0, relaydt_44_p5
  LED led_22 (.in(relaydt_44_p5));
  // RelayDT #(.poles(2)) relaydt_45: pin names not known; wires that end beside it: relaydt_41_p9, 1'b1, relaydt_25_p4, 1'b0, relaydt_45_p5
  // RelayDT #(.poles(2)) relaydt_46: pin names not known; wires that end beside it: relaydt_42_p9, 1'b1, relaydt_27_p4, 1'b0, relaydt_46_p5
  // RelayDT #(.poles(2)) relaydt_47: pin names not known; wires that end beside it: relaydt_41_p9, relaydt_26_p1, 1'b0, 1'b0, B_1, relaydt_47_p6, relaydt_47_p6, B_0, relaydt_47_p9, 1'b0, relaydt_47_p9, 1'b0
  // RelayDT #(.poles(2)) relaydt_48: pin names not known; wires that end beside it: relaydt_47_p6, 1'b1, relaydt_25_p4, 1'b0, relaydt_48_p5
  LED led_23 (.in(relaydt_45_p5));
  // RelayDT #(.poles(2)) relaydt_49: pin names not known; wires that end beside it: relaydt_42_p9, relaydt_28_p1, 1'b0, 1'b0, B_1, relaydt_49_p6, relaydt_49_p6, B_0, relaydt_49_p9, 1'b0, relaydt_49_p9, 1'b0
  // RelayDT #(.poles(2)) relaydt_50: pin names not known; wires that end beside it: relaydt_49_p6, 1'b1, relaydt_27_p4, 1'b0, relaydt_50_p5
  LED led_24 (.in(relaydt_46_p5));
  // RelayDT #(.poles(2)) relaydt_51: pin names not known; wires that end beside it: relaydt_47_p9, 1'b1, relaydt_25_p4, 1'b0, relaydt_51_p5
  LED led_25 (.in(relaydt_48_p5));
  // RelayDT #(.poles(2)) relaydt_52: pin names not known; wires that end beside it: relaydt_49_p9, 1'b1, relaydt_27_p4, 1'b0, relaydt_52_p5
  LED led_26 (.in(relaydt_50_p5));
  LED led_27 (.in(relaydt_51_p5));
  LED led_28 (.in(relaydt_52_p5));

  // Other names for the same wires on the sheet: L_0 = LOAD[0]; L_1 = LOAD[1]; L_2 = LOAD[2]; L_3 = LOAD[3];
  //   L_4 = LOAD[4]; L_5 = LOAD[5]; S_0 = SELECT[0]; S_1 = SELECT[1]; S_2 = SELECT[2]; S_3 = SELECT[3];
  //   S_4 = SELECT[4]; S_5 = SELECT[5]

  // Notes on the sheet:
  //   PC
  //   REGA
  //   BUS
endmodule
